// Logisim project Score Recorder-Done.circ as structural Verilog: 16 circuits, main circuit 系统集成
module \灯效驱动  (
  input  S0,
  input  S1,
  output L1,
  output L2
);

  or or_1 (L1, S1, S0);

  assign L2 = S1;
endmodule

module \数码管驱动  (
  input  X0,
  input  X1,
  input  X2,
  input  X3,
  output seg_1,
  output seg_2,
  output seg_3,
  output seg_4,
  output seg_5,
  output seg_6,
  output seg_7
);

  wire and_1_out, and_2_out, and_3_out, and_4_out, and_5_out, and_6_out, and_7_out, and_8_out, and_9_out,
       and_10_out, and_11_out, and_12_out, and_13_out, and_14_out, and_15_out, and_16_out, and_17_out,
       and_18_out, and_19_out, not_1_out, not_2_out, not_3_out, not_4_out, not_5_out, not_6_out, not_7_out,
       not_8_out, not_9_out, not_10_out, not_11_out, not_12_out, not_13_out, not_14_out, not_15_out,
       not_16_out, not_17_out, not_18_out, not_19_out, not_20_out, not_21_out, not_22_out, not_23_out;

  not not_1 (not_1_out, X3);
  and and_1 (and_1_out, not_1_out, not_2_out, X1);
  not not_2 (not_2_out, X2);
  and and_2 (and_2_out, X2, not_3_out);
  not not_3 (not_3_out, X1);
  and and_3 (and_3_out, X2, not_4_out);
  not not_4 (not_4_out, X0);
  and and_4 (and_4_out, X3, not_5_out);
  not not_5 (not_5_out, X1);
  and and_5 (and_5_out, X3, X2);
  not not_6 (not_6_out, X0);
  and and_6 (and_6_out, not_6_out, not_7_out);
  not not_7 (not_7_out, X1);
  not not_8 (not_8_out, X0);
  and and_7 (and_7_out, not_8_out, X2);
  not not_9 (not_9_out, X1);
  and and_8 (and_8_out, not_9_out, X2);
  not not_10 (not_10_out, X0);
  and and_9 (and_9_out, not_10_out, not_11_out);
  not not_11 (not_11_out, X2);
  and and_10 (and_10_out, X0, X2);
  not not_12 (not_12_out, X0);
  and and_11 (and_11_out, not_12_out, not_13_out);
  not not_13 (not_13_out, X1);
  not not_14 (not_14_out, X2);
  and and_12 (and_12_out, X0, X1);
  not not_15 (not_15_out, X0);
  and and_13 (and_13_out, not_15_out, not_16_out);
  not not_16 (not_16_out, X2);
  and and_14 (and_14_out, X2, X3);
  not not_17 (not_17_out, X0);
  and and_15 (and_15_out, not_17_out, X1);
  not not_18 (not_18_out, X0);
  and and_16 (and_16_out, not_18_out, not_19_out);
  not not_19 (not_19_out, X2);
  not not_20 (not_20_out, X0);
  and and_17 (and_17_out, not_20_out, X1);
  and and_18 (and_18_out, X1, not_21_out);
  not not_21 (not_21_out, X2);
  not not_22 (not_22_out, X1);
  and and_19 (and_19_out, X0, not_22_out, X2);
  not not_23 (not_23_out, X1);
  or or_1 (seg_1, and_1_out, and_2_out, and_3_out, and_4_out, and_5_out);
  or or_2 (seg_2, and_6_out, X3, and_7_out, and_8_out);
  or or_3 (seg_3, and_9_out, X3, X1, and_10_out);
  or or_4 (seg_4, and_11_out, not_14_out, X3, and_12_out);
  or or_5 (seg_5, and_13_out, and_14_out, and_15_out);
  or or_6 (seg_6, and_16_out, X3, and_17_out, and_18_out, and_19_out);
  or or_7 (seg_7, not_23_out, X3, X2, X0);
endmodule

module \二进制转BCD  (
  input  [3:0] binary,
  output [3:0] BCD_1,
  output [3:0] BCD_0
);

  // Probe on binary
  // Probe on BCD_1
  Divider #(.width(4)) divider_1 (.a(binary), .b(4'b1010), .out(BCD_1), .rem(BCD_0));  // open: upper
  // Probe on BCD_0

  // Notes on the sheet:
  //   输入引脚区
  //   输出引脚区
  //   输入1个4位二进制数（binary），将其转换为对应十进制数的十位（BCD_1）与个位（BCD_0）2个BCD码
endmodule

module \BCD逆向计数器输出函数  (
  input  S3,
  input  S2,
  input  S1,
  input  S0,
  output Cout
);

  wire not_1_out, not_2_out, not_3_out, not_4_out;

  not not_1 (not_1_out, S3);
  not not_2 (not_2_out, S2);
  not not_3 (not_3_out, S1);
  not not_4 (not_4_out, S0);
  and and_1 (Cout, not_1_out, not_2_out, not_3_out, not_4_out);

  // Notes on the sheet:
  //   逆向计数器输出函数，逢0输出借位信号Cout=1
endmodule

module \BCD逆向计数器状态转换  (
  input  S3,
  input  S2,
  input  S1,
  input  S0,
  output N3,
  output N2,
  output N1,
  output N0
);

  wire and_1_out, and_2_out, and_3_out, and_4_out, and_5_out, and_6_out, and_7_out, and_8_out, and_9_out,
       not_1_out, not_2_out, not_3_out, not_4_out, not_5_out, not_6_out, not_7_out, not_8_out, not_9_out,
       not_10_out, not_11_out, not_12_out;

  not not_1 (not_1_out, S3);
  not not_2 (not_2_out, S2);
  not not_3 (not_3_out, S1);
  not not_4 (not_4_out, S0);
  not not_5 (not_5_out, S2);
  not not_6 (not_6_out, S1);
  not not_7 (not_7_out, S2);
  not not_8 (not_8_out, S0);
  and and_1 (and_1_out, S2, S0);
  and and_2 (and_2_out, S2, S1);
  and and_3 (and_3_out, S3, not_9_out);
  not not_9 (not_9_out, S0);
  and and_4 (and_4_out, S1, S0);
  and and_5 (and_5_out, S2, not_10_out, not_11_out);
  not not_10 (not_10_out, S1);
  not not_11 (not_11_out, S0);
  and and_6 (and_6_out, S3, not_12_out);
  not not_12 (not_12_out, S0);
  not not_13 (N0, S0);
  and and_7 (and_7_out, not_1_out, not_2_out, not_3_out, not_4_out);
  or or_1 (N3, and_7_out, and_8_out, and_9_out);
  and and_8 (and_8_out, S3, not_5_out, not_6_out, S0);
  and and_9 (and_9_out, S3, not_7_out, S1, not_8_out);
  or or_2 (N2, and_1_out, and_2_out, and_3_out);
  or or_3 (N1, and_4_out, and_5_out, and_6_out);
endmodule

module \_4位BCD逆向计数器  (
  input  CLK,
  input  en,
  input  rst,
  input  [3:0] set,
  output [3:0] Q,
  output Cout
);

  wire and_1_out, \bcd逆向计数器状态转换_1_n0 , \bcd逆向计数器状态转换_1_n1 , \bcd逆向计数器状态转换_1_n2 , \bcd逆向计数器状态转换_1_n3 ,
       demultiplexer_1_out0, demultiplexer_1_out1, demultiplexer_2_out0, demultiplexer_2_out1,
       demultiplexer_3_out0, demultiplexer_3_out1, demultiplexer_4_out0, demultiplexer_4_out1, not_1_out;

  \BCD逆向计数器状态转换  \bcd逆向计数器状态转换_1  (
    .S3(Q[3]), .S2(Q[2]), .S1(Q[1]), .N3(\bcd逆向计数器状态转换_1_n3 ), .S0(Q[0]), .N2(\bcd逆向计数器状态转换_1_n2 ),
    .N1(\bcd逆向计数器状态转换_1_n1 ), .N0(\bcd逆向计数器状态转换_1_n0 ));
  and and_1 (and_1_out, CLK, not_1_out);
  not not_1 (not_1_out, rst);
  D_Flip_Flop #(.trigger("rising"), .Pre_Clr_Positions("LEGACY"), .NegatePresetClear("false"), .enable("true"), .NewFFLayout("false")) d_ff_1 (
    .clk(and_1_out), .D(\bcd逆向计数器状态转换_1_n3 ), .Q(Q[3]), .preset(demultiplexer_1_out1), .en(en),
    .reset(demultiplexer_1_out0));  // open: Qn
  Demultiplexer #(.select(1), .width(1), .tristate("false"), .disabled("Z"), .enable("false")) demultiplexer_1 (
    .out0(demultiplexer_1_out0), .out1(demultiplexer_1_out1), .in(rst), .sel(set[3]));
  D_Flip_Flop #(.trigger("rising"), .Pre_Clr_Positions("LEGACY"), .NegatePresetClear("false"), .enable("true"), .NewFFLayout("false")) d_ff_2 (
    .clk(and_1_out), .D(\bcd逆向计数器状态转换_1_n2 ), .Q(Q[2]), .preset(demultiplexer_2_out1), .en(en),
    .reset(demultiplexer_2_out0));  // open: Qn
  Demultiplexer #(.select(1), .width(1), .tristate("false"), .disabled("Z"), .enable("false")) demultiplexer_2 (
    .out0(demultiplexer_2_out0), .out1(demultiplexer_2_out1), .in(rst), .sel(set[2]));
  Demultiplexer #(.select(1), .width(1), .tristate("false"), .disabled("Z"), .enable("false")) demultiplexer_3 (
    .out0(demultiplexer_3_out0), .out1(demultiplexer_3_out1), .in(rst), .sel(set[1]));
  D_Flip_Flop #(.trigger("rising"), .Pre_Clr_Positions("LEGACY"), .NegatePresetClear("false"), .enable("true"), .NewFFLayout("false")) d_ff_3 (
    .clk(and_1_out), .D(\bcd逆向计数器状态转换_1_n1 ), .Q(Q[1]), .preset(demultiplexer_3_out1), .en(en),
    .reset(demultiplexer_3_out0));  // open: Qn
  D_Flip_Flop #(.trigger("rising"), .Pre_Clr_Positions("LEGACY"), .NegatePresetClear("false"), .enable("true"), .NewFFLayout("false")) d_ff_4 (
    .clk(and_1_out), .D(\bcd逆向计数器状态转换_1_n0 ), .Q(Q[0]), .preset(demultiplexer_4_out1), .en(en),
    .reset(demultiplexer_4_out0));  // open: Qn
  Demultiplexer #(.select(1), .width(1), .tristate("false"), .disabled("Z"), .enable("false")) demultiplexer_4 (
    .out0(demultiplexer_4_out0), .out1(demultiplexer_4_out1), .in(rst), .sel(set[0]));
  \BCD逆向计数器输出函数  \bcd逆向计数器输出函数_1  (.S3(Q[3]), .Cout(Cout), .S2(Q[2]), .S1(Q[1]), .S0(Q[0]));

  // Notes on the sheet:
  //   输入引脚区
  //   CLK：时钟信号
  //   en：使能信号
  //   rst：将计数器重置为set的值
  //   set：设置逆向计数起始值
  //   输出引脚区
  //   当en=1，则每一次时钟脉冲进行一次逆向计数，且逢0输出结尾信号Cout=1
  //   使用set设置0~15为起始值，设定好起始值后使用rst信号将计数器重置为set的值
  //   使用前面自动生成的状态转换与输出函数电路，结合触发器等元件，搭建可以设置起始值的逆向计数器
  //   Q：当前数值
  //   Cout：借位信号
endmodule

module \计时器  (
  input  CLK,
  input  en,
  input  rst,
  input  [3:0] \time ,
  output [3:0] Q1,
  output [3:0] Q0,
  output zero
);

  wire and_1_out, and_2_out, and_3_out, and_4_out, clock_1_out, comparator_1_eq, comparator_2_eq,
       \n4位bcd逆向计数器_2_cout , \n4位bcd逆向计数器_3_cout , \n4位bcd逆向计数器_4_cout , not_1_out;
  wire [3:0] \n4位bcd逆向计数器_3_q , \n4位bcd逆向计数器_4_q , \二进制转bcd_1_bcd_0 , \二进制转bcd_1_bcd_1 ;

  // Probe on \time 
  Clock #(.highDuration(1), .lowDuration(1)) clock_1 (.out(clock_1_out));
  not not_1 (not_1_out, zero);
  and and_1 (and_1_out, en, not_1_out);
  \二进制转BCD  \u_二进制转bcd_1  (.binary(\time ), .BCD_1(\二进制转bcd_1_bcd_1 ), .BCD_0(\二进制转bcd_1_bcd_0 ));
  and and_2 (and_2_out, \n4位bcd逆向计数器_2_cout , \n4位bcd逆向计数器_3_cout , \n4位bcd逆向计数器_4_cout , and_1_out);
  and and_3 (and_3_out, \n4位bcd逆向计数器_3_cout , \n4位bcd逆向计数器_4_cout , and_1_out);
  and and_4 (and_4_out, and_1_out, \n4位bcd逆向计数器_4_cout );
  // Probe on Q1
  \_4位BCD逆向计数器  \u_4位bcd逆向计数器_1  (
    .CLK(clock_1_out), .en(and_2_out), .rst(rst), .Q(Q1), .set(\二进制转bcd_1_bcd_1 ));  // open: Cout
  \_4位BCD逆向计数器  \u_4位bcd逆向计数器_2  (
    .CLK(clock_1_out), .en(and_3_out), .rst(rst), .Q(Q0), .Cout(\n4位bcd逆向计数器_2_cout ), .set(\二进制转bcd_1_bcd_0 ));
  \_4位BCD逆向计数器  \u_4位bcd逆向计数器_3  (
    .CLK(clock_1_out), .en(and_4_out), .rst(rst), .Q(\n4位bcd逆向计数器_3_q ), .Cout(\n4位bcd逆向计数器_3_cout ),
    .set(4'b0000));
  \_4位BCD逆向计数器  \u_4位bcd逆向计数器_4  (
    .CLK(clock_1_out), .en(and_1_out), .rst(rst), .Q(\n4位bcd逆向计数器_4_q ), .Cout(\n4位bcd逆向计数器_4_cout ),
    .set(4'b0000));
  // Probe on Q0
  // Probe on Q1
  // Probe on Q0
  // Probe on \n4位bcd逆向计数器_3_q 
  // Probe on \n4位bcd逆向计数器_4_q 
  Comparator #(.width(4), .mode("unsigned")) comparator_1 (.a(Q1), .b(4'b0000), .eq(comparator_1_eq));  // open: gt, lt
  Comparator #(.width(4), .mode("unsigned")) comparator_2 (.a(Q0), .b(4'b0000), .eq(comparator_2_eq));  // open: gt, lt
  and and_5 (zero, comparator_1_eq, comparator_2_eq);

  // Notes on the sheet:
  //   输入引脚区
  //   en：使能信号
  //   CLK：时钟信号
  //   rst：将计时器重置为time的值
  //   time：倒计时的秒数，使用4位二进制数输入
  //   低位计数器逢0则向相邻高位借1，所有计数器均为0则倒计时结束，zero=1
  //   当en=1则进行倒计时，当rst=1则将倒计时设置为time对应的十进制秒数；输出剩余秒数的整数部分
  //   输出引脚区
  //   使用4个BCD逆向计数器以及必要元件搭建倒计时计时器，4个逆向计数器对应10s、1s、0.1s、0.01s
  //   zero：倒计时结束信号
  //   Q1：剩余秒数（十进制）的十位数BCD码
  //   Q0：剩余秒数（十进制）的个位数BCD码
endmodule

module \分数锁存器状态转换电路  (
  input  S0,
  input  S1,
  input  B1,
  input  B2,
  output N0,
  output N1
);

  wire and_1_out, and_2_out, and_3_out, and_4_out, not_1_out, not_2_out, not_3_out, not_4_out, not_5_out,
       not_6_out, not_7_out, not_8_out;

  not not_1 (not_1_out, S0);
  and and_1 (and_1_out, not_1_out, B1, not_2_out);
  not not_2 (not_2_out, B2);
  and and_2 (and_2_out, S0, not_3_out, not_4_out);
  not not_3 (not_3_out, S1);
  not not_4 (not_4_out, B2);
  not not_5 (not_5_out, S1);
  not not_6 (not_6_out, B1);
  and and_3 (and_3_out, not_5_out, not_6_out, B2);
  not not_7 (not_7_out, S0);
  and and_4 (and_4_out, not_7_out, S1, not_8_out);
  not not_8 (not_8_out, B1);
  or or_1 (N0, and_1_out, and_2_out);
  or or_2 (N1, and_3_out, and_4_out);
endmodule

module \分数锁存器  (
  input  CLK,
  input  en,
  input  B1,
  input  B2,
  input  RST,
  output S0,
  output S1
);

  wire \分数锁存器状态转换电路_1_n0 , \分数锁存器状态转换电路_1_n1 ;

  \分数锁存器状态转换电路  \u_分数锁存器状态转换电路_1  (
    .S0(S0), .N0(\分数锁存器状态转换电路_1_n0 ), .S1(S1), .B1(B1), .B2(B2), .N1(\分数锁存器状态转换电路_1_n1 ));
  D_Flip_Flop #(.trigger("rising"), .Pre_Clr_Positions("LEGACY"), .NegatePresetClear("false"), .enable("true"), .NewFFLayout("false")) d_ff_1 (
    .clk(CLK), .D(\分数锁存器状态转换电路_1_n0 ), .Q(S0), .en(en), .reset(RST));  // open: Qn, preset
  D_Flip_Flop #(.trigger("rising"), .Pre_Clr_Positions("LEGACY"), .NegatePresetClear("false"), .enable("true"), .NewFFLayout("false")) d_ff_2 (
    .clk(CLK), .D(\分数锁存器状态转换电路_1_n1 ), .Q(S1), .en(en), .reset(RST));  // open: Qn, preset

  // Notes on the sheet:
  //   输入引脚区
  //   CLK：时钟信号
  //   en：使能信号
  //   RST：重置信号
  //   B1：按钮1的输入信号
  //   B2：按钮2的输入信号
  //   使用触发器等搭建分数锁存器，用于暂存评委的评分
  //   输出引脚区
  //   当en=1时可以暂存分数，当RST=1时则清空当前分数；当前分数通过S0（低位）S1（高位）输出
  //   评委使用2个按钮（B1、B2）进行评分，不按按钮为0分，仅按B1为1分，仅按B2为2分，同时按下B1、B2则将锁存器中分数归零
endmodule

module \分数计算器  (
  input  [1:0] S1,
  input  [1:0] S2,
  input  [1:0] S3,
  output [3:0] S
);

  wire [3:0] adder_1_out;

  // Probe on {2'b00, S1}
  Adder #(.width(4)) adder_1 (.a({2'b00, S1}), .b({2'b00, S2}), .out(adder_1_out));  // open: cin, cout
  // Probe on {2'b00, S2}
  // Probe on {2'b00, S3}
  // Probe on S
  Adder #(.width(4)) adder_2 (.a(adder_1_out), .b({2'b00, S3}), .out(S));  // open: cin, cout

  // Notes on the sheet:
  //   输入引脚区
  //   S1~S3：来自三个评委分数锁存器的分数（2bit二进制数）
  //   将3个2bit二进制数相加求和，以4bit二进制数（或BCD）输出和
  //   输出引脚区
  //   S：三个分数之和（4bit二进制数或BCD）
endmodule

module \_4位并行加载寄存器  (
  input  CLK,
  input  [3:0] Din,
  input  en,
  input  rst,
  output [3:0] Q
);

  D_Flip_Flop #(.trigger("rising"), .Pre_Clr_Positions("LEGACY"), .NegatePresetClear("false"), .enable("true"), .NewFFLayout("false")) d_ff_1 (
    .clk(CLK), .D(Din[0]), .Q(Q[0]), .en(en), .reset(rst));  // open: Qn, preset
  D_Flip_Flop #(.trigger("rising"), .Pre_Clr_Positions("LEGACY"), .NegatePresetClear("false"), .enable("true"), .NewFFLayout("false")) d_ff_2 (
    .clk(CLK), .D(Din[1]), .Q(Q[1]), .en(en), .reset(rst));  // open: Qn, preset
  D_Flip_Flop #(.trigger("rising"), .Pre_Clr_Positions("LEGACY"), .NegatePresetClear("false"), .enable("true"), .NewFFLayout("false")) d_ff_3 (
    .clk(CLK), .D(Din[2]), .Q(Q[2]), .en(en), .reset(rst));  // open: Qn, preset
  D_Flip_Flop #(.trigger("rising"), .Pre_Clr_Positions("LEGACY"), .NegatePresetClear("false"), .enable("true"), .NewFFLayout("false")) d_ff_4 (
    .clk(CLK), .D(Din[3]), .Q(Q[3]), .en(en), .reset(rst));  // open: Qn, preset

  // Notes on the sheet:
  //   输入引脚区
  //   rst=1时，清空该寄存器内数据为0
  //   CLK：时钟信号
  //   Din：4bit数据输入
  //   en：存储使能信号
  //   reset：重置信号
  //   使用4个触发器搭建4bit并行加载寄存器
  //   en=1时，来自Din的数据可以存入该寄存器
  //   输出引脚区
  //   Q：存储数据输出
endmodule

module \_10_4bit寄存器  (
  input  CLK,
  input  en,
  input  [3:0] Din,
  input  [3:0] Addr,
  input  rst,
  output [3:0] Q
);

  wire demultiplexer_2_out0, demultiplexer_2_out1, demultiplexer_2_out2, demultiplexer_2_out3,
       demultiplexer_2_out4, demultiplexer_2_out5, demultiplexer_2_out6, demultiplexer_2_out7,
       demultiplexer_2_out8, demultiplexer_2_out9;
  wire [3:0] demultiplexer_1_out0, demultiplexer_1_out1, demultiplexer_1_out2, demultiplexer_1_out3,
       demultiplexer_1_out4, demultiplexer_1_out5, demultiplexer_1_out6, demultiplexer_1_out7,
       demultiplexer_1_out8, demultiplexer_1_out9, \n4位并行加载寄存器_1_q , \n4位并行加载寄存器_2_q , \n4位并行加载寄存器_3_q ,
       \n4位并行加载寄存器_4_q , \n4位并行加载寄存器_5_q , \n4位并行加载寄存器_6_q , \n4位并行加载寄存器_7_q , \n4位并行加载寄存器_8_q ,
       \n4位并行加载寄存器_9_q , \n4位并行加载寄存器_10_q ;

  \_4位并行加载寄存器  \u_4位并行加载寄存器_1  (
    .CLK(CLK), .Din(demultiplexer_1_out0), .en(demultiplexer_2_out0), .Q(\n4位并行加载寄存器_1_q ), .rst(rst));
  \_4位并行加载寄存器  \u_4位并行加载寄存器_2  (
    .CLK(CLK), .Din(demultiplexer_1_out1), .en(demultiplexer_2_out1), .Q(\n4位并行加载寄存器_2_q ), .rst(rst));
  \_4位并行加载寄存器  \u_4位并行加载寄存器_3  (
    .CLK(CLK), .Din(demultiplexer_1_out2), .en(demultiplexer_2_out2), .Q(\n4位并行加载寄存器_3_q ), .rst(rst));
  \_4位并行加载寄存器  \u_4位并行加载寄存器_4  (
    .CLK(CLK), .Din(demultiplexer_1_out3), .en(demultiplexer_2_out3), .Q(\n4位并行加载寄存器_4_q ), .rst(rst));
  \_4位并行加载寄存器  \u_4位并行加载寄存器_5  (
    .CLK(CLK), .Din(demultiplexer_1_out4), .en(demultiplexer_2_out4), .Q(\n4位并行加载寄存器_5_q ), .rst(rst));
  Demultiplexer #(.select(4), .width(4), .tristate("false"), .disabled("Z"), .enable("false")) demultiplexer_1 (
    .out0(demultiplexer_1_out0), .out1(demultiplexer_1_out1), .out2(demultiplexer_1_out2),
    .out3(demultiplexer_1_out3), .out4(demultiplexer_1_out4), .out5(demultiplexer_1_out5),
    .out6(demultiplexer_1_out6), .out7(demultiplexer_1_out7), .out8(demultiplexer_1_out8),
    .out9(demultiplexer_1_out9), .in(Din), .sel(Addr));  // open: out10, out11, out12, out13, out14, out15
  Multiplexer #(.select(4), .width(4), .disabled("Z"), .enable("false")) multiplexer_1 (
    .in0(\n4位并行加载寄存器_1_q ), .in1(\n4位并行加载寄存器_2_q ), .in2(\n4位并行加载寄存器_3_q ), .in3(\n4位并行加载寄存器_4_q ),
    .in4(\n4位并行加载寄存器_5_q ), .in5(\n4位并行加载寄存器_6_q ), .in6(\n4位并行加载寄存器_7_q ), .in7(\n4位并行加载寄存器_8_q ),
    .in8(\n4位并行加载寄存器_9_q ), .in9(\n4位并行加载寄存器_10_q ), .out(Q), .sel(Addr));  // open: in10, in11, in12, in13, in14, in15
  \_4位并行加载寄存器  \u_4位并行加载寄存器_6  (
    .CLK(CLK), .Din(demultiplexer_1_out5), .en(demultiplexer_2_out5), .Q(\n4位并行加载寄存器_6_q ), .rst(rst));
  \_4位并行加载寄存器  \u_4位并行加载寄存器_7  (
    .CLK(CLK), .Din(demultiplexer_1_out6), .en(demultiplexer_2_out6), .Q(\n4位并行加载寄存器_7_q ), .rst(rst));
  \_4位并行加载寄存器  \u_4位并行加载寄存器_8  (
    .CLK(CLK), .Din(demultiplexer_1_out7), .en(demultiplexer_2_out7), .Q(\n4位并行加载寄存器_8_q ), .rst(rst));
  \_4位并行加载寄存器  \u_4位并行加载寄存器_9  (
    .CLK(CLK), .Din(demultiplexer_1_out8), .en(demultiplexer_2_out8), .Q(\n4位并行加载寄存器_9_q ), .rst(rst));
  \_4位并行加载寄存器  \u_4位并行加载寄存器_10  (
    .CLK(CLK), .Din(demultiplexer_1_out9), .en(demultiplexer_2_out9), .Q(\n4位并行加载寄存器_10_q ), .rst(rst));
  Demultiplexer #(.select(4), .width(1), .tristate("false"), .disabled("Z"), .enable("false")) demultiplexer_2 (
    .out0(demultiplexer_2_out0), .out1(demultiplexer_2_out1), .out2(demultiplexer_2_out2),
    .out3(demultiplexer_2_out3), .out4(demultiplexer_2_out4), .out5(demultiplexer_2_out5),
    .out6(demultiplexer_2_out6), .out7(demultiplexer_2_out7), .out8(demultiplexer_2_out8),
    .out9(demultiplexer_2_out9), .in(en), .sel(Addr));  // open: out10, out11, out12, out13, out14, out15

  // Notes on the sheet:
  //   利用10个4位并行加载寄存器和多路选择器、解复用器搭建10*4bit存储器
  //   en=1时，可将Din保存至Addr对应的4位并行加载寄存器中而不影响其他寄存器内的数据
  //   Addr可以选定将数据存入某片寄存器或从中读取数据
  //   rst=1则将所有寄存器清空为0
  //   输入引脚区
  //   CLK：时钟信号
  //   rst：重置信号
  //   en：存储使能信号
  //   Din：4bit数据输入
  //   Addr：4bit地址输入
  //   输出引脚区
  //   Q：对应地址的寄存器数据输出
endmodule

module \控制电路状态转换  (
  input  S0,
  input  S1,
  input  S2,
  input  start,
  input  over,
  input  store,
  input  show,
  input  reset,
  output N0,
  output N1,
  output N2
);

  wire and_1_out, and_2_out, and_3_out, and_4_out, and_5_out, and_6_out, and_7_out, and_8_out, and_9_out,
       and_10_out, and_11_out, and_12_out, and_13_out, and_14_out, and_15_out, and_16_out, and_17_out,
       and_18_out, and_19_out, and_20_out, and_21_out, not_1_out, not_2_out, not_3_out, not_4_out, not_5_out,
       not_6_out, not_7_out, not_8_out, not_9_out, not_10_out, not_11_out, not_12_out, not_13_out,
       not_14_out, not_15_out, not_16_out, not_17_out, not_18_out, not_19_out, not_20_out, not_21_out,
       not_22_out, not_23_out, not_24_out, not_25_out, not_26_out, not_27_out, not_28_out, not_29_out,
       not_30_out, not_31_out, not_32_out, not_33_out, not_34_out, not_35_out, not_36_out, not_37_out,
       not_38_out, not_39_out, not_40_out, not_41_out, not_42_out, not_43_out, not_44_out, not_45_out,
       not_46_out, not_47_out, not_48_out, not_49_out, not_50_out, not_51_out, not_52_out, not_53_out,
       not_54_out, not_55_out, not_56_out, not_57_out, not_58_out, not_59_out, not_60_out, not_61_out,
       not_62_out, not_63_out, not_64_out, not_65_out, not_66_out, not_67_out, not_68_out, not_69_out,
       not_70_out, not_71_out, not_72_out, not_73_out, not_74_out;

  not not_1 (not_1_out, S2);
  not not_2 (not_2_out, S1);
  not not_3 (not_3_out, S0);
  not not_4 (not_4_out, S2);
  not not_5 (not_5_out, S1);
  not not_6 (not_6_out, start);
  not not_7 (not_7_out, show);
  not not_8 (not_8_out, reset);
  not not_9 (not_9_out, S2);
  not not_10 (not_10_out, S1);
  not not_11 (not_11_out, start);
  not not_12 (not_12_out, reset);
  not not_13 (not_13_out, S2);
  not not_14 (not_14_out, S0);
  not not_15 (not_15_out, reset);
  not not_16 (not_16_out, S2);
  not not_17 (not_17_out, store);
  not not_18 (not_18_out, show);
  not not_19 (not_19_out, reset);
  not not_20 (not_20_out, S2);
  not not_21 (not_21_out, store);
  not not_22 (not_22_out, reset);
  not not_23 (not_23_out, S1);
  not not_24 (not_24_out, S0);
  not not_25 (not_25_out, reset);
  not not_26 (not_26_out, S1);
  not not_27 (not_27_out, store);
  not not_28 (not_28_out, show);
  not not_29 (not_29_out, reset);
  not not_30 (not_30_out, S1);
  not not_31 (not_31_out, store);
  not not_32 (not_32_out, reset);
  not not_33 (not_33_out, S2);
  not not_34 (not_34_out, S1);
  not not_35 (not_35_out, show);
  not not_36 (not_36_out, reset);
  not not_37 (not_37_out, S2);
  not not_38 (not_38_out, S0);
  not not_39 (not_39_out, over);
  not not_40 (not_40_out, reset);
  not not_41 (not_41_out, S2);
  not not_42 (not_42_out, S0);
  not not_43 (not_43_out, reset);
  not not_44 (not_44_out, S2);
  not not_45 (not_45_out, store);
  not not_46 (not_46_out, show);
  not not_47 (not_47_out, reset);
  not not_48 (not_48_out, S2);
  not not_49 (not_49_out, S1);
  not not_50 (not_50_out, start);
  not not_51 (not_51_out, reset);
  not not_52 (not_52_out, S2);
  not not_53 (not_53_out, show);
  not not_54 (not_54_out, reset);
  not not_55 (not_55_out, S2);
  not not_56 (not_56_out, store);
  not not_57 (not_57_out, reset);
  not not_58 (not_58_out, S1);
  not not_59 (not_59_out, S0);
  not not_60 (not_60_out, show);
  not not_61 (not_61_out, reset);
  not not_62 (not_62_out, S1);
  not not_63 (not_63_out, S0);
  not not_64 (not_64_out, reset);
  not not_65 (not_65_out, S1);
  not not_66 (not_66_out, store);
  not not_67 (not_67_out, show);
  not not_68 (not_68_out, reset);
  not not_69 (not_69_out, S1);
  not not_70 (not_70_out, show);
  not not_71 (not_71_out, reset);
  not not_72 (not_72_out, S1);
  not not_73 (not_73_out, store);
  not not_74 (not_74_out, reset);
  and and_1 (and_1_out, not_1_out, not_2_out, not_3_out);
  and and_2 (and_2_out, not_4_out, not_5_out, S0, not_6_out, not_7_out, not_8_out);
  and and_3 (and_3_out, not_9_out, not_10_out, S0, not_11_out, show, not_12_out);
  and and_4 (and_4_out, not_13_out, S1, not_14_out, over, not_15_out);
  and and_5 (and_5_out, not_16_out, S1, S0, not_17_out, not_18_out, not_19_out);
  and and_6 (and_6_out, not_20_out, S1, S0, not_21_out, show, not_22_out);
  and and_7 (and_7_out, S2, not_23_out, not_24_out, show, not_25_out);
  and and_8 (and_8_out, S2, not_26_out, S0, not_27_out, not_28_out, not_29_out);
  and and_9 (and_9_out, S2, not_30_out, S0, not_31_out, show, not_32_out);
  and and_10 (and_10_out, not_33_out, not_34_out, S0, start, not_35_out, not_36_out);
  and and_11 (and_11_out, not_37_out, S1, not_38_out, not_39_out, not_40_out);
  and and_12 (and_12_out, not_41_out, S1, not_42_out, over, not_43_out);
  and and_13 (and_13_out, not_44_out, S1, S0, not_45_out, not_46_out, not_47_out);
  and and_14 (and_14_out, not_48_out, not_49_out, S0, not_50_out, show, not_51_out);
  and and_15 (and_15_out, not_52_out, S1, S0, store, not_53_out, not_54_out);
  and and_16 (and_16_out, not_55_out, S1, S0, not_56_out, show, not_57_out);
  and and_17 (and_17_out, S2, not_58_out, not_59_out, not_60_out, not_61_out);
  and and_18 (and_18_out, S2, not_62_out, not_63_out, show, not_64_out);
  and and_19 (and_19_out, S2, not_65_out, S0, not_66_out, not_67_out, not_68_out);
  and and_20 (and_20_out, S2, not_69_out, S0, store, not_70_out, not_71_out);
  and and_21 (and_21_out, S2, not_72_out, S0, not_73_out, show, not_74_out);
  or or_1 (N0, and_1_out, and_2_out, and_3_out, and_4_out, and_5_out, and_6_out, and_7_out, and_8_out, and_9_out);
  or or_2 (N1, and_10_out, and_11_out, and_12_out, and_13_out);
  or or_3 (N2, and_14_out, and_15_out, and_16_out, and_17_out, and_18_out, and_19_out, and_20_out, and_21_out);
endmodule

module \控制电路输出函数  (
  input  S0,
  input  S1,
  input  S2,
  output TimeEn,
  output JudgeEn,
  output StoreEn,
  output ShowEn,
  output RST
);

  wire not_1_out, not_2_out, not_3_out, not_4_out, not_5_out, not_6_out, not_7_out, not_8_out, not_9_out,
       not_10_out;

  not not_1 (not_1_out, S0);
  not not_2 (not_2_out, S2);
  not not_3 (not_3_out, S0);
  not not_4 (not_4_out, S2);
  not not_5 (not_5_out, S0);
  not not_6 (not_6_out, S1);
  not not_7 (not_7_out, S1);
  not not_8 (not_8_out, S0);
  not not_9 (not_9_out, S1);
  not not_10 (not_10_out, S2);
  and and_1 (TimeEn, not_1_out, S1, not_2_out);
  and and_2 (JudgeEn, not_3_out, S1, not_4_out);
  and and_3 (StoreEn, not_5_out, not_6_out, S2);
  and and_4 (ShowEn, S0, not_7_out, S2);
  and and_5 (RST, not_8_out, not_9_out, not_10_out);
endmodule

module \控制电路  (
  input  CLK,
  input  start,
  input  over,
  input  store,
  input  show,
  input  rst,
  output TimeEn,
  output JudgeEn,
  output StoreEn,
  output ShowEn,
  output RST_2
);

  wire d_ff_1_q, d_ff_2_q, d_ff_3_q, \控制电路状态转换_1_n0 , \控制电路状态转换_1_n1 , \控制电路状态转换_1_n2 ;

  \控制电路状态转换  \u_控制电路状态转换_1  (
    .S0(d_ff_1_q), .S1(d_ff_2_q), .S2(d_ff_3_q), .start(start), .over(over), .store(store), .show(show),
    .reset(rst), .N0(\控制电路状态转换_1_n0 ), .N1(\控制电路状态转换_1_n1 ), .N2(\控制电路状态转换_1_n2 ));
  D_Flip_Flop #(.trigger("rising"), .Pre_Clr_Positions("LEGACY"), .NegatePresetClear("false"), .enable("false"), .NewFFLayout("false")) d_ff_1 (
    .clk(CLK), .D(\控制电路状态转换_1_n0 ), .Q(d_ff_1_q));  // open: Qn, preset, reset
  D_Flip_Flop #(.trigger("rising"), .Pre_Clr_Positions("LEGACY"), .NegatePresetClear("false"), .enable("false"), .NewFFLayout("false")) d_ff_2 (
    .clk(CLK), .D(\控制电路状态转换_1_n1 ), .Q(d_ff_2_q));  // open: Qn, preset, reset
  D_Flip_Flop #(.trigger("rising"), .Pre_Clr_Positions("LEGACY"), .NegatePresetClear("false"), .enable("false"), .NewFFLayout("false")) d_ff_3 (
    .clk(CLK), .D(\控制电路状态转换_1_n2 ), .Q(d_ff_3_q));  // open: Qn, preset, reset
  \控制电路输出函数  \u_控制电路输出函数_1  (
    .S0(d_ff_1_q), .TimeEn(TimeEn), .S1(d_ff_2_q), .JudgeEn(JudgeEn), .S2(d_ff_3_q), .StoreEn(StoreEn),
    .ShowEn(ShowEn), .RST(RST_2));

  // Other names for the same wires on the sheet: RST_t = RST_2

  // Notes on the sheet:
  //   输入引脚区
  //   使用自动生成的状态转换电路与输出函数电路，结合触发器搭建控制电路
  //   使之能在输入信号下完成正确的状态转换与信号输出
  //   CLK：时钟信号
  //   start：开始计时与评分
  //   over：结束计时与评分
  //   store：存储评分
  //   show：查看评分
  //   rst：重置
  //   输出引脚区
  //   TimeEn：计时使能
  //   JudgeEn：评分使能
  //   StoreEn：存储使能
  //   ShowEn：查看使能
  //   RST：重置使能
endmodule

module \系统集成  (
);

  wire ClearData, CLK, comparator_1_lt, J1B1, J1B2, J1L1, J1L2, J2B1, J2B2, J2L1, J2L2, J3B1, J3B2, J3L1,
       J3L2, JudgeEn, JudgeNext, or_1_out, or_2_out, Pass, reset, RST, show, ShowEn, start, stop, store,
       StoreEn, TimeEn, zero;
  wire [1:0] \分数锁存器_1_s0 , \分数锁存器_2_s0 , \分数锁存器_3_s0 ;
  wire [3:0] adder_1_out, multiplexer_1_out, multiplexer_2_out, multiplexer_3_out, multiplexer_4_out, Num,
       NumDown, NumUp, Score, ShowNum, ShowScore, SocreDown, SocreUp, T0, T0down, T0up, T1, T1down, T1up,
       TMset;

  Button u_start (.out(start));
  Button u_stop (.out(stop));
  Button u_store (.out(store));
  Button u_show (.out(show));
  Button u_reset (.out(reset));
  Clock #(.highDuration(1), .lowDuration(1)) clock_1 (.out(CLK));
  or or_1 (or_1_out, ClearData, RST);
  _7_Segment_Display #(.active("true")) u_7_segment_display_1 (
    .g(NumUp[0]), .f(NumUp[1]), .a(NumUp[2]), .b(NumUp[3]), .e(NumDown[0]), .d(NumDown[1]), .c(NumDown[2]),
    .dp(NumDown[3]));
  Counter #(.width(4), .max('h9), .ongoal("wrap"), .trigger("rising"), .behavior("new")) counter_1 (
    .Q(Num), .clk(JudgeNext), .clr(ClearData));  // open: load, D, count, carry, preset, down
  \分数锁存器  \u_分数锁存器_1  (
    .CLK(CLK), .en(JudgeEn), .B1(J1B1), .B2(J1B2), .RST(or_1_out), .S0(\分数锁存器_1_s0 [0]), .S1(\分数锁存器_1_s0 [1]));
  \分数锁存器  \u_分数锁存器_2  (
    .CLK(CLK), .en(JudgeEn), .B1(J2B1), .B2(J2B2), .RST(or_1_out), .S0(\分数锁存器_2_s0 [0]), .S1(\分数锁存器_2_s0 [1]));
  \分数锁存器  \u_分数锁存器_3  (
    .CLK(CLK), .en(JudgeEn), .B1(J3B1), .B2(J3B2), .RST(or_1_out), .S0(\分数锁存器_3_s0 [0]), .S1(\分数锁存器_3_s0 [1]));
  _7_Segment_Display #(.active("true")) u_7_segment_display_2 (
    .g(SocreUp[0]), .f(SocreUp[1]), .a(SocreUp[2]), .b(SocreUp[3]), .e(SocreDown[0]), .d(SocreDown[1]),
    .c(SocreDown[2]), .dp(SocreDown[3]));
  LED #(.active("true")) led_1 (.in(Pass));
  Slider #(.width(4), .Direction("left_to_right"), .value('ha)) slider_1 (.out(TMset));
  \计时器  \u_计时器_1  (.CLK(CLK), .en(TimeEn), .rst(RST), .\time (TMset), .Q1(T1), .Q0(T0), .zero(zero));
  \分数计算器  \u_分数计算器_1  (.S1(\分数锁存器_1_s0 ), .S2(\分数锁存器_2_s0 ), .S3(\分数锁存器_3_s0 ), .S(Score));
  _7_Segment_Display #(.active("true")) u_7_segment_display_3 (
    .g(T0up[0]), .f(T0up[1]), .a(T0up[2]), .b(T0up[3]), .e(T0down[0]), .d(T0down[1]), .c(T0down[2]),
    .dp(T0down[3]));
  _7_Segment_Display #(.active("true")) u_7_segment_display_4 (
    .g(T1up[0]), .f(T1up[1]), .a(T1up[2]), .b(T1up[3]), .e(T1down[0]), .d(T1down[1]), .c(T1down[2]),
    .dp(T1down[3]));
  \灯效驱动  \u_灯效驱动_1  (.S0(\分数锁存器_1_s0 [0]), .L1(J1L1), .S1(\分数锁存器_1_s0 [1]), .L2(J1L2));
  \灯效驱动  \u_灯效驱动_2  (.S0(\分数锁存器_2_s0 [0]), .L1(J2L1), .S1(\分数锁存器_2_s0 [1]), .L2(J2L2));
  \灯效驱动  \u_灯效驱动_3  (.S0(\分数锁存器_3_s0 [0]), .L1(J3L1), .S1(\分数锁存器_3_s0 [1]), .L2(J3L2));
  LED #(.active("true")) led_2 (.in(J1L1));
  LED #(.active("true")) led_3 (.in(J1L2));
  Button u_J1B1 (.out(J1B1));
  Button u_J1B2 (.out(J1B2));
  \数码管驱动  \u_数码管驱动_1  (
    .X0(T1[0]), .X1(T1[1]), .X2(T1[2]), .seg_1(T1up[0]), .X3(T1[3]), .seg_2(T1up[1]), .seg_3(T1up[2]),
    .seg_4(T1up[3]), .seg_5(T1down[0]), .seg_6(T1down[1]), .seg_7(T1down[2]));
  \数码管驱动  \u_数码管驱动_2  (
    .X0(T0[0]), .X1(T0[1]), .X2(T0[2]), .seg_1(T0up[0]), .X3(T0[3]), .seg_2(T0up[1]), .seg_3(T0up[2]),
    .seg_4(T0up[3]), .seg_5(T0down[0]), .seg_6(T0down[1]), .seg_7(T0down[2]));
  Adder #(.width(4)) adder_1 (.a(4'b0001), .b(Num), .out(adder_1_out));  // open: cin, cout
  Multiplexer #(.select(1), .width(4), .disabled("Z"), .enable("false")) multiplexer_1 (
    .in0(adder_1_out), .in1(Num), .out(multiplexer_1_out), .sel(JudgeNext));
  LED #(.active("true")) led_4 (.in(J2L1));
  Button u_J2B1 (.out(J2B1));
  Multiplexer #(.select(1), .width(4), .disabled("Z"), .enable("false")) multiplexer_2 (
    .in0(Score), .in1(ShowScore), .out(multiplexer_2_out), .sel(ShowEn));
  Multiplexer #(.select(1), .width(4), .disabled("Z"), .enable("false")) multiplexer_3 (
    .in0(multiplexer_1_out), .in1(ShowNum), .out(multiplexer_3_out), .sel(ShowEn));
  LED #(.active("true")) led_5 (.in(J2L2));
  Button u_J2B2 (.out(J2B2));
  Comparator #(.width(4), .mode("unsigned")) comparator_1 (
    .a(multiplexer_2_out), .b(4'b0100), .lt(comparator_1_lt));  // open: gt, eq
  LED #(.active("true")) led_6 (.in(J3L1));
  LED #(.active("true")) led_7 (.in(J3L2));
  Button u_J3B2 (.out(J3B2));
  Button u_J3B1 (.out(J3B1));
  \数码管驱动  \u_数码管驱动_3  (
    .X0(multiplexer_2_out[0]), .X1(multiplexer_2_out[1]), .X2(multiplexer_2_out[2]), .seg_1(SocreUp[0]),
    .X3(multiplexer_2_out[3]), .seg_2(SocreUp[1]), .seg_3(SocreUp[2]), .seg_4(SocreUp[3]),
    .seg_5(SocreDown[0]), .seg_6(SocreDown[1]), .seg_7(SocreDown[2]));
  not not_1 (Pass, comparator_1_lt);
  \数码管驱动  \u_数码管驱动_4  (
    .X0(multiplexer_3_out[0]), .X1(multiplexer_3_out[1]), .X2(multiplexer_3_out[2]), .seg_1(NumUp[0]),
    .X3(multiplexer_3_out[3]), .seg_2(NumUp[1]), .seg_3(NumUp[2]), .seg_4(NumUp[3]), .seg_5(NumDown[0]),
    .seg_6(NumDown[1]), .seg_7(NumDown[2]));
  or or_2 (or_2_out, zero, stop);
  Multiplexer #(.select(1), .width(4), .disabled("Z"), .enable("false")) multiplexer_4 (
    .in0(Num), .in1(ShowNum), .out(multiplexer_4_out), .sel(ShowEn));
  Button u_ClearData (.out(ClearData));
  D_Flip_Flop #(.trigger("rising"), .Pre_Clr_Positions("LEGACY"), .NegatePresetClear("false"), .enable("false"), .NewFFLayout("false")) d_ff_1 (
    .clk(CLK), .Q(JudgeNext), .preset(StoreEn), .reset(RST));  // open: D, Qn
  \_10_4bit寄存器  \u_10_4bit寄存器_1  (
    .CLK(CLK), .Din(Score), .en(StoreEn), .Addr(multiplexer_4_out), .Q(ShowScore), .rst(ClearData));
  Counter #(.width(4), .max('h9), .ongoal("wrap"), .trigger("rising"), .behavior("new")) counter_2 (
    .Q(ShowNum), .clk(show), .clr(ClearData));  // open: load, D, count, carry, preset, down
  \控制电路  \u_控制电路_1  (
    .CLK(CLK), .start(start), .over(or_2_out), .store(store), .show(show), .rst(reset), .TimeEn(TimeEn),
    .JudgeEn(JudgeEn), .StoreEn(StoreEn), .ShowEn(ShowEn), .RST_2(RST));

  // Notes on the sheet:
  //   主持人面板
  //   后台计时模块
  //   后台计分模块
  //   显示面板驱动模块
  //   评委面板
  //   后台控制模块
  //   成绩存储读取模块
endmodule
