// Logisim project ScoreRecorder - 电路框架.circ as structural Verilog: 16 circuits, main circuit 系统集成
module \灯效驱动  (
  input  S0,
  input  S1,
  output L1,
  output L2
);
endmodule

module \数码管驱动  (
  input  X0,
  input  X1,
  input  X2,
  input  X3,
  output seg_1,
  output seg_2,
  output seg_3,
  output seg_4,
  output seg_5,
  output seg_6,
  output seg_7
);
endmodule

module \二进制转BCD  (
  input  [3:0] binary,
  output [3:0] BCD_1,
  output [3:0] BCD_0
);


  // Notes on the sheet:
  //   输入引脚区
  //   输出引脚区
  //   输入1个4位二进制数（binary），将其转换为对应十进制数的十位（BCD_1）与个位（BCD_0）2个BCD码
endmodule

module \BCD逆向计数器输出函数  (
  input  S3,
  input  S2,
  input  S1,
  input  S0,
  output Cout
);


  // Notes on the sheet:
  //   逆向计数器输出函数，逢0输出借位信号Cout=1
endmodule

module \BCD逆向计数器状态转换  (
  input  S3,
  input  S2,
  input  S1,
  input  S0,
  output N3,
  output N2,
  output N1,
  output N0
);
endmodule

module \_4位BCD逆向计数器  (
  input  CLK,
  input  en,
  input  rst,
  input  [3:0] set,
  output [3:0] Q,
  output Cout
);

  \BCD逆向计数器状态转换  \bcd逆向计数器状态转换_1  ();  // open: S3, S2, S1, N3, S0, N2, N1, N0
  D_Flip_Flop #(.trigger("rising"), .Pre_Clr_Positions("LEGACY"), .NegatePresetClear("false"), .enable("true"), .NewFFLayout("false")) d_ff_1 ();  // open: clk, D, Q, Qn, preset, en, reset
  D_Flip_Flop #(.trigger("rising"), .Pre_Clr_Positions("LEGACY"), .NegatePresetClear("false"), .enable("true"), .NewFFLayout("false")) d_ff_2 ();  // open: clk, D, Q, Qn, preset, en, reset
  D_Flip_Flop #(.trigger("rising"), .Pre_Clr_Positions("LEGACY"), .NegatePresetClear("false"), .enable("true"), .NewFFLayout("false")) d_ff_3 ();  // open: clk, D, Q, Qn, preset, en, reset
  \BCD逆向计数器输出函数  \bcd逆向计数器输出函数_1  ();  // open: S3, Cout, S2, S1, S0
  D_Flip_Flop #(.trigger("rising"), .Pre_Clr_Positions("LEGACY"), .NegatePresetClear("false"), .enable("true"), .NewFFLayout("false")) d_ff_4 ();  // open: clk, D, Q, Qn, preset, en, reset

  // Notes on the sheet:
  //   输入引脚区
  //   CLK：时钟信号
  //   en：使能信号
  //   rst：将计数器重置为set的值
  //   set：设置逆向计数起始值
  //   输出引脚区
  //   当en=1，则每一次时钟脉冲进行一次逆向计数，且逢0输出结尾信号Cout=1
  //   使用set设置0~15为起始值，设定好起始值后使用rst信号将计数器重置为set的值
  //   使用前面自动生成的状态转换与输出函数电路，结合触发器等元件，搭建可以设置起始值的逆向计数器
  //   Q：当前数值
  //   Cout：借位信号
endmodule

module \计时器  (
  input  CLK,
  input  en,
  input  rst,
  input  [3:0] \time ,
  output [3:0] Q1,
  output [3:0] Q0,
  output zero
);

  // Probe on \time 
  \二进制转BCD  \u_二进制转bcd_1  ();  // open: binary, BCD_1, BCD_0
  // Probe on Q1
  \_4位BCD逆向计数器  \u_4位bcd逆向计数器_1  ();  // open: CLK, en, rst, Q, Cout, set
  \_4位BCD逆向计数器  \u_4位bcd逆向计数器_2  ();  // open: CLK, en, rst, Q, Cout, set
  \_4位BCD逆向计数器  \u_4位bcd逆向计数器_3  ();  // open: CLK, en, rst, Q, Cout, set
  \_4位BCD逆向计数器  \u_4位bcd逆向计数器_4  ();  // open: CLK, en, rst, Q, Cout, set
  // Probe on Q0
  Comparator #(.width(4), .mode("unsigned")) comparator_1 ();  // open: a, b, gt, eq, lt

  // Notes on the sheet:
  //   输入引脚区
  //   en：使能信号
  //   CLK：时钟信号
  //   rst：将计时器重置为time的值
  //   time：倒计时的秒数，使用4位二进制数输入
  //   低位计数器逢0则向相邻高位借1，所有计数器均为0则倒计时结束，zero=1
  //   当en=1则进行倒计时，当rst=1则将倒计时设置为time对应的十进制秒数；输出剩余秒数的整数部分
  //   输出引脚区
  //   使用4个BCD逆向计数器以及必要元件搭建倒计时计时器，4个逆向计数器对应10s、1s、0.1s、0.01s
  //   zero：倒计时结束信号
  //   Q1：剩余秒数（十进制）的十位数BCD码
  //   Q0：剩余秒数（十进制）的个位数BCD码
endmodule

module \分数锁存器状态转换电路  (
  input  S0,
  input  S1,
  input  B1,
  input  B2,
  output N0,
  output N1
);
endmodule

module \分数锁存器  (
  input  CLK,
  input  en,
  input  B1,
  input  B2,
  input  RST,
  output S0,
  output S1
);

  \分数锁存器状态转换电路  \u_分数锁存器状态转换电路_1  ();  // open: S0, N0, S1, B1, B2, N1
  D_Flip_Flop #(.trigger("rising"), .Pre_Clr_Positions("LEGACY"), .NegatePresetClear("false"), .enable("true"), .NewFFLayout("false")) d_ff_1 ();  // open: clk, D, Q, Qn, preset, en, reset
  D_Flip_Flop #(.trigger("rising"), .Pre_Clr_Positions("LEGACY"), .NegatePresetClear("false"), .enable("true"), .NewFFLayout("false")) d_ff_2 ();  // open: clk, D, Q, Qn, preset, en, reset

  // Notes on the sheet:
  //   输入引脚区
  //   CLK：时钟信号
  //   en：使能信号
  //   RST：重置信号
  //   B1：按钮1的输入信号
  //   B2：按钮2的输入信号
  //   使用触发器等搭建分数锁存器，用于暂存评委的评分
  //   输出引脚区
  //   当en=1时可以暂存分数，当RST=1时则清空当前分数；当前分数通过S0（低位）S1（高位）输出
  //   评委使用2个按钮（B1、B2）进行评分，不按按钮为0分，仅按B1为1分，仅按B2为2分，同时按下B1、B2则将锁存器中分数归零
endmodule

module \分数计算器  (
  input  [1:0] S1,
  input  [1:0] S2,
  input  [1:0] S3,
  output [3:0] S
);


  // Notes on the sheet:
  //   输入引脚区
  //   S1~S3：来自三个评委分数锁存器的分数（2bit二进制数）
  //   将3个2bit二进制数相加求和，以4bit二进制数（或BCD）输出和
  //   输出引脚区
  //   S：三个分数之和（4bit二进制数或BCD）
endmodule

module \_4位并行加载寄存器  (
  input  CLK,
  input  [3:0] Din,
  input  en,
  input  rst,
  output [3:0] Q
);

  D_Flip_Flop #(.trigger("rising"), .Pre_Clr_Positions("LEGACY"), .NegatePresetClear("false"), .enable("true"), .NewFFLayout("false")) d_ff_1 ();  // open: clk, D, Q, Qn, preset, en, reset
  D_Flip_Flop #(.trigger("rising"), .Pre_Clr_Positions("LEGACY"), .NegatePresetClear("false"), .enable("true"), .NewFFLayout("false")) d_ff_2 ();  // open: clk, D, Q, Qn, preset, en, reset
  D_Flip_Flop #(.trigger("rising"), .Pre_Clr_Positions("LEGACY"), .NegatePresetClear("false"), .enable("true"), .NewFFLayout("false")) d_ff_3 ();  // open: clk, D, Q, Qn, preset, en, reset
  D_Flip_Flop #(.trigger("rising"), .Pre_Clr_Positions("LEGACY"), .NegatePresetClear("false"), .enable("true"), .NewFFLayout("false")) d_ff_4 ();  // open: clk, D, Q, Qn, preset, en, reset

  // Notes on the sheet:
  //   输入引脚区
  //   rst=1时，清空该寄存器内数据为0
  //   CLK：时钟信号
  //   Din：4bit数据输入
  //   en：存储使能信号
  //   reset：重置信号
  //   使用4个触发器搭建4bit并行加载寄存器
  //   en=1时，来自Din的数据可以存入该寄存器
  //   输出引脚区
  //   Q：存储数据输出
endmodule

module \_10_4bit寄存器  (
  input  CLK,
  input  en,
  input  [3:0] Din,
  input  [3:0] Addr,
  input  rst,
  output [3:0] Q
);

  \_4位并行加载寄存器  \u_4位并行加载寄存器_1  ();  // open: CLK, Din, en, Q, rst
  \_4位并行加载寄存器  \u_4位并行加载寄存器_2  ();  // open: CLK, Din, en, Q, rst
  \_4位并行加载寄存器  \u_4位并行加载寄存器_3  ();  // open: CLK, Din, en, Q, rst
  \_4位并行加载寄存器  \u_4位并行加载寄存器_4  ();  // open: CLK, Din, en, Q, rst
  \_4位并行加载寄存器  \u_4位并行加载寄存器_5  ();  // open: CLK, Din, en, Q, rst
  Demultiplexer #(.select(4), .width(4), .tristate("false"), .disabled("Z"), .enable("false")) demultiplexer_1 ();  // open: out0, out1, out2, out3, out4, out5, out6, out7, out8, out9, out10, out11, out12, out13, out14, out15, in, sel
  \_4位并行加载寄存器  \u_4位并行加载寄存器_6  ();  // open: CLK, Din, en, Q, rst
  \_4位并行加载寄存器  \u_4位并行加载寄存器_7  ();  // open: CLK, Din, en, Q, rst
  \_4位并行加载寄存器  \u_4位并行加载寄存器_8  ();  // open: CLK, Din, en, Q, rst
  \_4位并行加载寄存器  \u_4位并行加载寄存器_9  ();  // open: CLK, Din, en, Q, rst
  \_4位并行加载寄存器  \u_4位并行加载寄存器_10  ();  // open: CLK, Din, en, Q, rst

  // Notes on the sheet:
  //   利用10个4位并行加载寄存器和多路选择器、解复用器搭建10*4bit存储器
  //   en=1时，可将Din保存至Addr对应的4位并行加载寄存器中而不影响其他寄存器内的数据
  //   Addr可以选定将数据存入某片寄存器或从中读取数据
  //   rst=1则将所有寄存器清空为0
  //   输入引脚区
  //   CLK：时钟信号
  //   rst：重置信号
  //   en：存储使能信号
  //   Din：4bit数据输入
  //   Addr：4bit地址输入
  //   输出引脚区
  //   Q：对应地址的寄存器数据输出
endmodule

module \控制电路状态转换  (
  input  S0,
  input  S1,
  input  S2,
  input  start,
  input  over,
  input  store,
  input  show,
  input  reset,
  output N0,
  output N1,
  output N2
);
endmodule

module \控制电路输出函数  (
  input  S0,
  input  S1,
  input  S2,
  output TimeEn,
  output JudgeEn,
  output StoreEn,
  output ShowEn,
  output RST
);
endmodule

module \控制电路  (
  input  CLK,
  input  start,
  input  over,
  input  store,
  input  show,
  input  rst,
  output TimeEn,
  output JudgeEn,
  output StoreEn,
  output ShowEn,
  output RST_2
);

  \控制电路状态转换  \u_控制电路状态转换_1  ();  // open: S0, N0, S1, N1, S2, N2, start, over, store, show, reset
  D_Flip_Flop #(.trigger("rising"), .Pre_Clr_Positions("LEGACY"), .NegatePresetClear("false"), .enable("false"), .NewFFLayout("false")) d_ff_1 ();  // open: clk, D, Q, Qn, preset, reset
  D_Flip_Flop #(.trigger("rising"), .Pre_Clr_Positions("LEGACY"), .NegatePresetClear("false"), .enable("false"), .NewFFLayout("false")) d_ff_2 ();  // open: clk, D, Q, Qn, preset, reset
  D_Flip_Flop #(.trigger("rising"), .Pre_Clr_Positions("LEGACY"), .NegatePresetClear("false"), .enable("false"), .NewFFLayout("false")) d_ff_3 ();  // open: clk, D, Q, Qn, preset, reset
  \控制电路输出函数  \u_控制电路输出函数_1  ();  // open: S0, TimeEn, S1, JudgeEn, S2, StoreEn, ShowEn, RST

  // Other names for the same wires on the sheet: RST_t = RST_2

  // Notes on the sheet:
  //   输入引脚区
  //   使用自动生成的状态转换电路与输出函数电路，结合触发器搭建控制电路
  //   使之能在输入信号下完成正确的状态转换与信号输出
  //   CLK：时钟信号
  //   start：开始计时与评分
  //   over：结束计时与评分
  //   store：存储评分
  //   show：查看评分
  //   rst：重置
  //   输出引脚区
  //   TimeEn：计时使能
  //   JudgeEn：评分使能
  //   StoreEn：存储使能
  //   ShowEn：查看使能
  //   RST：重置使能
endmodule

module \系统集成  (
);

  wire ClearData, CLK, comparator_1_lt, J1B1, J1B2, J1L1, J1L2, J2B1, J2B2, J2L1, J2L2, J3B1, J3B2, J3L1,
       J3L2, JudgeEn, JudgeNext, or_1_out, or_2_out, Pass, reset, RST, show, ShowEn, start, stop, store,
       StoreEn, TimeEn, zero;
  wire [1:0] \分数锁存器_1_s0 , \分数锁存器_2_s0 , \分数锁存器_3_s0 ;
  wire [3:0] adder_1_out, multiplexer_1_out, multiplexer_2_out, multiplexer_3_out, multiplexer_4_out, Num,
       NumDown, NumUp, Score, ShowNum, ShowScore, SocreDown, SocreUp, T0, T0down, T0up, T1, T1down, T1up,
       TMset;

  Button u_start (.out(start));
  Button u_stop (.out(stop));
  Button u_store (.out(store));
  Button u_show (.out(show));
  Button u_reset (.out(reset));
  Clock #(.highDuration(1), .lowDuration(1)) clock_1 (.out(CLK));
  or or_1 (or_1_out, ClearData, RST);
  _7_Segment_Display #(.active("true")) u_7_segment_display_1 (
    .g(NumUp[0]), .f(NumUp[1]), .a(NumUp[2]), .b(NumUp[3]), .e(NumDown[0]), .d(NumDown[1]), .c(NumDown[2]),
    .dp(NumDown[3]));
  Counter #(.width(4), .max('h9), .ongoal("wrap"), .trigger("rising"), .behavior("new")) counter_1 (
    .Q(Num), .clk(JudgeNext), .clr(ClearData));  // open: load, D, count, carry, preset, down
  \分数锁存器  \u_分数锁存器_1  (
    .CLK(CLK), .en(JudgeEn), .B1(J1B1), .B2(J1B2), .RST(or_1_out), .S0(\分数锁存器_1_s0 [0]), .S1(\分数锁存器_1_s0 [1]));
  \分数锁存器  \u_分数锁存器_2  (
    .CLK(CLK), .en(JudgeEn), .B1(J2B1), .B2(J2B2), .RST(or_1_out), .S0(\分数锁存器_2_s0 [0]), .S1(\分数锁存器_2_s0 [1]));
  \分数锁存器  \u_分数锁存器_3  (
    .CLK(CLK), .en(JudgeEn), .B1(J3B1), .B2(J3B2), .RST(or_1_out), .S0(\分数锁存器_3_s0 [0]), .S1(\分数锁存器_3_s0 [1]));
  _7_Segment_Display #(.active("true")) u_7_segment_display_2 (
    .g(SocreUp[0]), .f(SocreUp[1]), .a(SocreUp[2]), .b(SocreUp[3]), .e(SocreDown[0]), .d(SocreDown[1]),
    .c(SocreDown[2]), .dp(SocreDown[3]));
  LED #(.active("true")) led_1 (.in(Pass));
  Slider #(.width(4), .Direction("left_to_right"), .value('ha)) slider_1 (.out(TMset));
  \计时器  \u_计时器_1  (.CLK(CLK), .en(TimeEn), .rst(RST), .\time (TMset), .Q1(T1), .Q0(T0), .zero(zero));
  \分数计算器  \u_分数计算器_1  (.S1(\分数锁存器_1_s0 ), .S2(\分数锁存器_2_s0 ), .S3(\分数锁存器_3_s0 ), .S(Score));
  _7_Segment_Display #(.active("true")) u_7_segment_display_3 (
    .g(T1up[0]), .f(T1up[1]), .a(T1up[2]), .b(T1up[3]), .e(T1down[0]), .d(T1down[1]), .c(T1down[2]),
    .dp(T1down[3]));
  _7_Segment_Display #(.active("true")) u_7_segment_display_4 (
    .g(T0up[0]), .f(T0up[1]), .a(T0up[2]), .b(T0up[3]), .e(T0down[0]), .d(T0down[1]), .c(T0down[2]),
    .dp(T0down[3]));
  \灯效驱动  \u_灯效驱动_1  (.S0(\分数锁存器_1_s0 [0]), .L1(J1L1), .S1(\分数锁存器_1_s0 [1]), .L2(J1L2));
  \灯效驱动  \u_灯效驱动_2  (.S0(\分数锁存器_2_s0 [0]), .L1(J2L1), .S1(\分数锁存器_2_s0 [1]), .L2(J2L2));
  \灯效驱动  \u_灯效驱动_3  (.S0(\分数锁存器_3_s0 [0]), .L1(J3L1), .S1(\分数锁存器_3_s0 [1]), .L2(J3L2));
  LED #(.active("true")) led_2 (.in(J1L1));
  LED #(.active("true")) led_3 (.in(J1L2));
  Button u_J1B2 (.out(J1B2));
  Button u_J1B1 (.out(J1B1));
  \数码管驱动  \u_数码管驱动_1  (
    .X0(T1[0]), .X1(T1[1]), .X2(T1[2]), .seg_1(T1up[0]), .X3(T1[3]), .seg_2(T1up[1]), .seg_3(T1up[2]),
    .seg_4(T1up[3]), .seg_5(T1down[0]), .seg_6(T1down[1]), .seg_7(T1down[2]));
  \数码管驱动  \u_数码管驱动_2  (
    .X0(T0[0]), .X1(T0[1]), .X2(T0[2]), .seg_1(T0up[0]), .X3(T0[3]), .seg_2(T0up[1]), .seg_3(T0up[2]),
    .seg_4(T0up[3]), .seg_5(T0down[0]), .seg_6(T0down[1]), .seg_7(T0down[2]));
  Adder #(.width(4)) adder_1 (.a(4'b0001), .b(Num), .out(adder_1_out));  // open: cin, cout
  Multiplexer #(.select(1), .width(4), .disabled("Z"), .enable("false")) multiplexer_1 (
    .in0(adder_1_out), .in1(Num), .out(multiplexer_1_out), .sel(JudgeNext));
  LED #(.active("true")) led_4 (.in(J2L1));
  Button u_J2B1 (.out(J2B1));
  Multiplexer #(.select(1), .width(4), .disabled("Z"), .enable("false")) multiplexer_2 (
    .in0(Score), .in1(ShowScore), .out(multiplexer_2_out), .sel(ShowEn));
  Multiplexer #(.select(1), .width(4), .disabled("Z"), .enable("false")) multiplexer_3 (
    .in0(multiplexer_1_out), .in1(ShowNum), .out(multiplexer_3_out), .sel(ShowEn));
  LED #(.active("true")) led_5 (.in(J2L2));
  Button u_J2B2 (.out(J2B2));
  Comparator #(.width(4), .mode("unsigned")) comparator_1 (
    .a(multiplexer_2_out), .b(4'b0100), .lt(comparator_1_lt));  // open: gt, eq
  LED #(.active("true")) led_6 (.in(J3L2));
  LED #(.active("true")) led_7 (.in(J3L1));
  Button u_J3B1 (.out(J3B1));
  Button u_J3B2 (.out(J3B2));
  \数码管驱动  \u_数码管驱动_3  (
    .X0(multiplexer_2_out[0]), .X1(multiplexer_2_out[1]), .X2(multiplexer_2_out[2]), .seg_1(SocreUp[0]),
    .X3(multiplexer_2_out[3]), .seg_2(SocreUp[1]), .seg_3(SocreUp[2]), .seg_4(SocreUp[3]),
    .seg_5(SocreDown[0]), .seg_6(SocreDown[1]), .seg_7(SocreDown[2]));
  not not_1 (Pass, comparator_1_lt);
  \数码管驱动  \u_数码管驱动_4  (
    .X0(multiplexer_3_out[0]), .X1(multiplexer_3_out[1]), .X2(multiplexer_3_out[2]), .seg_1(NumUp[0]),
    .X3(multiplexer_3_out[3]), .seg_2(NumUp[1]), .seg_3(NumUp[2]), .seg_4(NumUp[3]), .seg_5(NumDown[0]),
    .seg_6(NumDown[1]), .seg_7(NumDown[2]));
  or or_2 (or_2_out, zero, stop);
  Multiplexer #(.select(1), .width(4), .disabled("Z"), .enable("false")) multiplexer_4 (
    .in0(Num), .in1(ShowNum), .out(multiplexer_4_out), .sel(ShowEn));
  Button u_ClearData (.out(ClearData));
  D_Flip_Flop #(.trigger("rising"), .Pre_Clr_Positions("LEGACY"), .NegatePresetClear("false"), .enable("false"), .NewFFLayout("false")) d_ff_1 (
    .clk(CLK), .Q(JudgeNext), .preset(StoreEn), .reset(RST));  // open: D, Qn
  \_10_4bit寄存器  \u_10_4bit寄存器_1  (
    .CLK(CLK), .Din(Score), .en(StoreEn), .Addr(multiplexer_4_out), .Q(ShowScore), .rst(ClearData));
  Counter #(.width(4), .max('h9), .ongoal("wrap"), .trigger("rising"), .behavior("new")) counter_2 (
    .Q(ShowNum), .clk(show), .clr(ClearData));  // open: load, D, count, carry, preset, down
  \控制电路  \u_控制电路_1  (
    .CLK(CLK), .start(start), .over(or_2_out), .store(store), .show(show), .rst(reset), .TimeEn(TimeEn),
    .JudgeEn(JudgeEn), .StoreEn(StoreEn), .ShowEn(ShowEn), .RST_2(RST));

  // Notes on the sheet:
  //   主持人面板
  //   后台计时模块
  //   后台计分模块
  //   显示面板驱动模块
  //   评委面板
  //   后台控制模块
  //   成绩存储读取模块
endmodule
