// Logisim project 01-LED_driver_test.circ as structural Verilog: 1 circuit, main circuit 灯效驱动测试
module \灯效驱动测试  (
  output [1:0] Cnt,
  output S0,
  output S1,
  output L1,
  output L2,
  output _passed,
  output halt
);

  wire CLK, nhalt;
  wire [1:0] OutputS;

  Clock #(.highDuration(1), .lowDuration(1)) clock_1 (.out(CLK));
  Comparator #(.width(2), .mode("twosComplement")) comparator_1 (.a(Cnt), .b(2'b11), .eq(halt));  // open: gt, lt
  not not_1 (nhalt, halt);
  Counter #(.width(2), .max('h3), .ongoal("wrap"), .trigger("rising"), .behavior("old")) counter_1 (
    .count(nhalt), .Q(Cnt), .clk(CLK));  // open: load, D, carry, clr, preset
  ROM #(.addrWidth(2), .dataWidth(2), .Select("low")) rom_1 (.addr(Cnt), .data({S1, S0}));
  ROM #(.addrWidth(2), .dataWidth(2), .Select("low")) rom_2 (.addr(Cnt), .data(OutputS));
  \灯效驱动  \u_灯效驱动_1  (.S0(S0), .L1(L1), .S1(S1), .L2(L2));
  Comparator #(.width(2), .mode("twosComplement")) comparator_2 (
    .a({L2, L1}), .b(OutputS), .eq(_passed));  // open: gt, lt
  Pull_Resistor #(.pull(0)) pull_resistor_1 (.node(_passed));

  // Other names for the same wires on the sheet: Equal = _passed; Input[1:0] = {S1, S0}; Out[1:0] = {L2, L1};
  //   tunnel[1:0] = Cnt

  // Notes on the sheet:
  //   contents of rom_1 (hex, n*v repeats v):
  //   0 1 2 3
  //   contents of rom_2 (hex, n*v repeats v):
  //   0 1 3 3
endmodule
