// Logisim project 02-Digital_driver_test.circ as structural Verilog: 1 circuit, main circuit 数码管驱动测试
module \数码管驱动测试  (
  output [15:0] Cnt,
  output [3:0] BCD,
  output [6:0] _7Segs,
  output _passed,
  output halt
);

  wire CLK, nhalt, \数码管驱动_2_seg_1 , \数码管驱动_2_seg_2 , \数码管驱动_2_seg_3 , \数码管驱动_2_seg_4 , \数码管驱动_2_seg_5 ,
       \数码管驱动_2_seg_6 , \数码管驱动_2_seg_7 ;
  wire [6:0] OutputS;

  Clock #(.highDuration(1), .lowDuration(1)) clock_1 (.out(CLK));
  Comparator #(.width(16), .mode("twosComplement")) comparator_1 (.a(Cnt), .b(16'h9), .eq(halt));  // open: gt, lt
  not not_1 (nhalt, halt);
  Counter #(.width(16), .max('ha), .ongoal("wrap"), .trigger("rising"), .behavior("old")) counter_1 (
    .count(nhalt), .Q(Cnt), .clk(CLK));  // open: load, D, carry, clr, preset
  ROM #(.addrWidth(16), .dataWidth(4), .Select("low")) rom_1 (.addr(Cnt), .data(BCD));
  ROM #(.addrWidth(16), .dataWidth(7), .Select("low")) rom_2 (.addr(Cnt), .data(OutputS));
  RAM #(.addrWidth(16), .dataWidth(7), .bus("separate"), .Select("low")) ram_1 (
    .addr(Cnt), .din(_7Segs), .str(nhalt), .clk(CLK));  // open: data, sel, ld, clr
  \数码管驱动  \u_数码管驱动_1  (
    .X0(BCD[0]), .X1(BCD[1]), .X2(BCD[2]), .seg_1(_7Segs[0]), .X3(BCD[3]), .seg_2(_7Segs[1]),
    .seg_3(_7Segs[2]), .seg_4(_7Segs[3]), .seg_5(_7Segs[4]), .seg_6(_7Segs[5]), .seg_7(_7Segs[6]));
  \数码管驱动  \u_数码管驱动_2  (
    .X0(BCD[0]), .X1(BCD[1]), .X2(BCD[2]), .seg_1(\数码管驱动_2_seg_1 ), .X3(BCD[3]), .seg_2(\数码管驱动_2_seg_2 ),
    .seg_3(\数码管驱动_2_seg_3 ), .seg_4(\数码管驱动_2_seg_4 ), .seg_5(\数码管驱动_2_seg_5 ), .seg_6(\数码管驱动_2_seg_6 ),
    .seg_7(\数码管驱动_2_seg_7 ));
  Comparator #(.width(7), .mode("twosComplement")) comparator_2 (
    .a(_7Segs), .b(OutputS), .eq(_passed));  // open: gt, lt
  _7_Segment_Display #(.active("true")) u_7_segment_display_1 (
    .g(\数码管驱动_2_seg_1 ), .f(\数码管驱动_2_seg_2 ), .a(\数码管驱动_2_seg_3 ), .b(\数码管驱动_2_seg_4 ), .e(\数码管驱动_2_seg_5 ),
    .d(\数码管驱动_2_seg_6 ), .c(\数码管驱动_2_seg_7 ));  // open: dp
  Pull_Resistor #(.pull(0)) pull_resistor_1 (.node(_passed));

  // Other names for the same wires on the sheet: Equal = _passed; Input[3:0] = BCD; Out[6:0] = _7Segs;
  //   tunnel[15:0] = Cnt

  // Notes on the sheet:
  //   contents of rom_1 (hex, n*v repeats v):
  //   0 1 2 3 4 5 6 7 8 9
  //   contents of rom_2 (hex, n*v repeats v):
  //   7e 48 3d 6d 4b 67 77 4c 7f 6f
endmodule
