// Logisim project 03-Binary_to_BCD_test.circ as structural Verilog: 1 circuit, main circuit 二进制转BCD测试
module \二进制转BCD测试  (
  output [3:0] Cnt,
  output [3:0] Binary,
  output [3:0] BCD_0,
  output [3:0] BCD_1,
  output _passed,
  output halt
);

  wire CLK, nhalt;
  wire [7:0] OutputS;

  Clock #(.highDuration(1), .lowDuration(1)) clock_1 (.out(CLK));
  Comparator #(.width(4), .mode("twosComplement")) comparator_1 (.a(Cnt), .b(4'b1111), .eq(halt));  // open: gt, lt
  not not_1 (nhalt, halt);
  Counter #(.width(4), .max('hf), .ongoal("wrap"), .trigger("rising"), .behavior("old")) counter_1 (
    .count(nhalt), .Q(Cnt), .clk(CLK));  // open: load, D, carry, clr, preset
  ROM #(.addrWidth(4), .dataWidth(4), .Select("low")) rom_1 (.addr(Cnt), .data(Binary));
  ROM #(.addrWidth(4), .dataWidth(8), .Select("low")) rom_2 (.addr(Cnt), .data(OutputS));
  RAM #(.addrWidth(4), .dataWidth(8), .bus("separate"), .Select("low")) ram_1 (
    .addr(Cnt), .din({BCD_1, BCD_0}), .str(nhalt), .clk(CLK));  // open: data, sel, ld, clr
  \二进制转BCD  \u_二进制转bcd_1  (.binary(Binary), .BCD_1(BCD_1), .BCD_0(BCD_0));
  Comparator #(.width(8), .mode("twosComplement")) comparator_2 (
    .a({BCD_1, BCD_0}), .b(OutputS), .eq(_passed));  // open: gt, lt
  Pull_Resistor #(.pull(0)) pull_resistor_1 (.node(_passed));

  // Other names for the same wires on the sheet: Equal = _passed; Input[3:0] = Binary; Out[7:0] = {BCD_1, BCD_0};
  //   tunnel[3:0] = Cnt

  // Notes on the sheet:
  //   contents of rom_1 (hex, n*v repeats v):
  //   0 1 2 3 4 5 6 7 8 9 a b c d e f
  //   contents of rom_2 (hex, n*v repeats v):
  //   0 1 2 3 4 5 6 7 8 9 10 11 12 13 14 15
endmodule
