// Logisim project 04-Counter_OutFunc_test.circ as structural Verilog: 1 circuit, main circuit BCD逆向计数器输出函数测试
module \BCD逆向计数器输出函数测试  (
  output [3:0] Cnt,
  output S3,
  output S2,
  output S1,
  output S0,
  output Cout,
  output _passed,
  output halt
);

  wire CLK, nhalt, OutputS;

  Clock #(.highDuration(1), .lowDuration(1)) clock_1 (.out(CLK));
  Comparator #(.width(4), .mode("twosComplement")) comparator_1 (.a(Cnt), .b(4'b1111), .eq(halt));  // open: gt, lt
  not not_1 (nhalt, halt);
  Counter #(.width(4), .max('hf), .ongoal("wrap"), .trigger("rising"), .behavior("old")) counter_1 (
    .count(nhalt), .Q(Cnt), .clk(CLK));  // open: load, D, carry, clr, preset
  ROM #(.addrWidth(4), .dataWidth(4), .Select("low")) rom_1 (.addr(Cnt), .data({S0, S1, S2, S3}));
  ROM #(.addrWidth(4), .dataWidth(1), .Select("low")) rom_2 (.addr(Cnt), .data(OutputS));
  RAM #(.addrWidth(4), .dataWidth(1), .bus("separate"), .Select("low")) ram_1 (
    .addr(Cnt), .din(Cout), .str(nhalt), .clk(CLK));  // open: data, sel, ld, clr
  \BCD逆向计数器输出函数  \bcd逆向计数器输出函数_1  (.S3(S3), .Cout(Cout), .S2(S2), .S1(S1), .S0(S0));
  Comparator #(.width(1), .mode("twosComplement")) comparator_2 (.a(Cout), .b(OutputS), .eq(_passed));  // open: gt, lt
  Pull_Resistor #(.pull(0)) pull_resistor_1 (.node(_passed));

  // Other names for the same wires on the sheet: Equal = _passed; Input[3:0] = {S0, S1, S2, S3}; Out = Cout;
  //   tunnel[3:0] = Cnt

  // Notes on the sheet:
  //   contents of rom_1 (hex, n*v repeats v):
  //   0 1 2 3 4 5 6 7 8 9 a b c d e f
  //   contents of rom_2 (hex, n*v repeats v):
  //   1
endmodule
