// Logisim project 05-Counter_FSM_test.circ as structural Verilog: 1 circuit, main circuit BCD逆向计数器状态转换测试
module \BCD逆向计数器状态转换测试  (
  output [3:0] Cnt,
  output S3,
  output S2,
  output S1,
  output S0,
  output N3,
  output N2,
  output N1,
  output N0,
  output _passed,
  output halt
);

  wire CLK, nhalt;
  wire [3:0] OutputS;

  Clock #(.highDuration(1), .lowDuration(1)) clock_1 (.out(CLK));
  Comparator #(.width(4), .mode("twosComplement")) comparator_1 (.a(Cnt), .b(4'b1111), .eq(halt));  // open: gt, lt
  not not_1 (nhalt, halt);
  Counter #(.width(4), .max('hf), .ongoal("wrap"), .trigger("rising"), .behavior("old")) counter_1 (
    .count(nhalt), .Q(Cnt), .clk(CLK));  // open: load, D, carry, clr, preset
  ROM #(.addrWidth(4), .dataWidth(4), .Select("low")) rom_1 (.addr(Cnt), .data({S3, S2, S1, S0}));
  ROM #(.addrWidth(4), .dataWidth(4), .Select("low")) rom_2 (.addr(Cnt), .data(OutputS));
  RAM #(.addrWidth(4), .dataWidth(4), .bus("separate"), .Select("low")) ram_1 (
    .addr(Cnt), .din({N3, N2, N1, N0}), .str(nhalt), .clk(CLK));  // open: data, sel, ld, clr
  \BCD逆向计数器状态转换  \bcd逆向计数器状态转换_1  (.S3(S3), .S2(S2), .S1(S1), .N3(N3), .S0(S0), .N2(N2), .N1(N1), .N0(N0));
  Comparator #(.width(4), .mode("twosComplement")) comparator_2 (
    .a({N3, N2, N1, N0}), .b(OutputS), .eq(_passed));  // open: gt, lt
  Pull_Resistor #(.pull(0)) pull_resistor_1 (.node(_passed));

  // Other names for the same wires on the sheet: Equal = _passed; Input[3:0] = {S3, S2, S1, S0};
  //   Out[3:0] = {N3, N2, N1, N0}; tunnel[3:0] = Cnt

  // Notes on the sheet:
  //   contents of rom_1 (hex, n*v repeats v):
  //   0 1 2 3 4 5 6 7 8 9 a b c d e f
  //   contents of rom_2 (hex, n*v repeats v):
  //   9 0 1 2 3 4 5 6 7 8 f 2 7 4 7 6
endmodule
