// Logisim project 06-Counter_test.circ as structural Verilog: 1 circuit, main circuit 4位BCD逆向计数器测试
module \_4位BCD逆向计数器测试  (
  output [7:0] Cnt,
  output en,
  output rst,
  output [3:0] set,
  output [3:0] Q,
  output Cout,
  output _passed,
  output halt
);

  wire CLK, nhalt;
  wire [4:0] OutputS;

  Clock #(.highDuration(1), .lowDuration(1)) clock_1 (.out(CLK));
  Comparator #(.width(8), .mode("twosComplement")) comparator_1 (.a(Cnt), .b({8{1'b1}}), .eq(halt));  // open: gt, lt
  not not_1 (nhalt, halt);
  Counter #(.width(8), .max('hff), .ongoal("wrap"), .trigger("rising"), .behavior("old")) counter_1 (
    .count(nhalt), .Q(Cnt), .clk(CLK));  // open: load, D, carry, clr, preset
  ROM #(.addrWidth(8), .dataWidth(4), .Select("low")) rom_1 (.addr(Cnt), .data(set));
  ROM #(.addrWidth(8), .dataWidth(1), .Select("low")) rom_2 (.addr(Cnt), .data(en));
  ROM #(.addrWidth(8), .dataWidth(1), .Select("low")) rom_3 (.addr(Cnt), .data(rst));
  ROM #(.addrWidth(8), .dataWidth(5), .Select("low")) rom_4 (.addr(Cnt), .data(OutputS));
  RAM #(.addrWidth(8), .dataWidth(5), .bus("separate"), .Select("low")) ram_1 (
    .addr(Cnt), .din({Cout, Q}), .str(nhalt), .clk(CLK));  // open: data, sel, ld, clr
  \_4位BCD逆向计数器  \u_4位bcd逆向计数器_1  (.CLK(CLK), .en(en), .rst(rst), .Q(Q), .Cout(Cout), .set(set));
  Comparator #(.width(5), .mode("twosComplement")) comparator_2 (
    .a({Cout, Q}), .b(OutputS), .eq(_passed));  // open: gt, lt
  Pull_Resistor #(.pull(0)) pull_resistor_1 (.node(_passed));

  // Other names for the same wires on the sheet: Equal = _passed; Out[4:0] = {Cout, Q}; tunnel[7:0] = Cnt

  // Notes on the sheet:
  //   contents of rom_1 (hex, n*v repeats v):
  //   256*9
  //   contents of rom_2 (hex, n*v repeats v):
  //   128*0 128*1
  //   contents of rom_3 (hex, n*v repeats v):
  //   64*1 128*0 64*1
  //   contents of rom_4 (hex, n*v repeats v):
  //   129*9 8 7 6 5 4 3 2 1 10 9 8 7 6 5 4 3 2 1 10 9 8 7 6 5 4 3 2 1 10 9 8 7 6 5 4 3 2 1 10 9 8 7 6 5 4
  //   3 2 1 10 9 8 7 6 5 4 3 2 1 10 9 8 7 6 64*9
endmodule
