// Logisim project 07-Timer_test.circ as structural Verilog: 1 circuit, main circuit 计时器测试
module \计时器测试  (
  output [11:0] Cnt,
  output en,
  output rst,
  output [3:0] \time ,
  output [3:0] Q1,
  output [3:0] Q0,
  output zero,
  output _passed,
  output halt
);

  wire CLK, nhalt;
  wire [8:0] OutputS;

  Clock #(.highDuration(1), .lowDuration(1)) clock_1 (.out(CLK));
  Comparator #(.width(12), .mode("twosComplement")) comparator_1 (.a(Cnt), .b(12'h7ff), .eq(halt));  // open: gt, lt
  not not_1 (nhalt, halt);
  Counter #(.width(12), .max('hfff), .ongoal("wrap"), .trigger("rising"), .behavior("old")) counter_1 (
    .count(nhalt), .Q(Cnt), .clk(CLK));  // open: load, D, carry, clr, preset
  ROM #(.addrWidth(12), .dataWidth(4), .Select("low")) rom_1 (.addr(Cnt), .data(\time ));
  ROM #(.addrWidth(12), .dataWidth(1), .Select("low")) rom_2 (.addr(Cnt), .data(en));
  ROM #(.addrWidth(12), .dataWidth(1), .Select("low")) rom_3 (.addr(Cnt), .data(rst));
  ROM #(.addrWidth(12), .dataWidth(9), .Select("low")) rom_4 (.addr(Cnt), .data(OutputS));
  RAM #(.addrWidth(12), .dataWidth(9), .bus("separate"), .Select("low")) ram_1 (
    .addr(Cnt), .din({zero, Q1, Q0}), .str(nhalt), .clk(CLK));  // open: data, sel, ld, clr
  \计时器  \u_计时器_1  (.CLK(CLK), .en(en), .rst(rst), .\time (\time ), .Q1(Q1), .Q0(Q0), .zero(zero));
  Comparator #(.width(9), .mode("twosComplement")) comparator_2 (
    .a({zero, Q1, Q0}), .b(OutputS), .eq(_passed));  // open: gt, lt
  Pull_Resistor #(.pull(0)) pull_resistor_1 (.node(_passed));

  // Other names for the same wires on the sheet: Equal = _passed; Out[8:0] = {zero, Q1, Q0}; tunnel[11:0] = Cnt

  // Notes on the sheet:
  //   contents of rom_1 (hex, n*v repeats v):
  //   4096*5
  //   contents of rom_2 (hex, n*v repeats v):
  //   1024*0 1024*1
  //   contents of rom_3 (hex, n*v repeats v):
  //   512*1 1024*0 512*1
  //   contents of rom_4 (hex, n*v repeats v):
  //   1025*5 100*4 100*3 100*2 100*1 111*100 512*5
endmodule
