// Logisim project 08-Score_Storage_FSM_test.circ as structural Verilog: 1 circuit, main circuit 分数锁存器状态转换测试
module \分数锁存器状态转换测试  (
  output [3:0] Cnt,
  output S0,
  output S1,
  output B1,
  output B2,
  output N0,
  output N1,
  output _passed,
  output halt
);

  wire CLK, nhalt;
  wire [1:0] OutputS;

  Clock #(.highDuration(1), .lowDuration(1)) clock_1 (.out(CLK));
  Comparator #(.width(4), .mode("twosComplement")) comparator_1 (.a(Cnt), .b(4'b1111), .eq(halt));  // open: gt, lt
  not not_1 (nhalt, halt);
  Counter #(.width(4), .max('hf), .ongoal("wrap"), .trigger("rising"), .behavior("old")) counter_1 (
    .count(nhalt), .Q(Cnt), .clk(CLK));  // open: load, D, carry, clr, preset
  ROM #(.addrWidth(4), .dataWidth(1), .Select("low")) rom_1 (.addr(Cnt), .data(S0));
  ROM #(.addrWidth(4), .dataWidth(1), .Select("low")) rom_2 (.addr(Cnt), .data(S1));
  ROM #(.addrWidth(4), .dataWidth(1), .Select("low")) rom_3 (.addr(Cnt), .data(B1));
  ROM #(.addrWidth(4), .dataWidth(1), .Select("low")) rom_4 (.addr(Cnt), .data(B2));
  ROM #(.addrWidth(4), .dataWidth(2), .Select("low")) rom_5 (.addr(Cnt), .data(OutputS));
  RAM #(.addrWidth(4), .dataWidth(2), .bus("separate"), .Select("low")) ram_1 (
    .addr(Cnt), .din({N1, N0}), .str(nhalt), .clk(CLK));  // open: data, sel, ld, clr
  \分数锁存器状态转换电路  \u_分数锁存器状态转换电路_1  (.S0(S0), .N0(N0), .S1(S1), .B1(B1), .B2(B2), .N1(N1));
  Comparator #(.width(2), .mode("twosComplement")) comparator_2 (
    .a({N1, N0}), .b(OutputS), .eq(_passed));  // open: gt, lt
  Pull_Resistor #(.pull(0)) pull_resistor_1 (.node(_passed));

  // Other names for the same wires on the sheet: Equal = _passed; Out[1:0] = {N1, N0}; tunnel[3:0] = Cnt

  // Notes on the sheet:
  //   contents of rom_1 (hex, n*v repeats v):
  //   0 1 0 1 0 1 0 1 0 1 0 1 0 1 0 1
  //   contents of rom_2 (hex, n*v repeats v):
  //   0 0 1 1 0 0 1 1 0 0 1 1 0 0 1 1
  //   contents of rom_3 (hex, n*v repeats v):
  //   4*0 4*1 4*0 4*1
  //   contents of rom_4 (hex, n*v repeats v):
  //   8*0 8*1
  //   contents of rom_5 (hex, n*v repeats v):
  //   0 1 2 0 1 1 1 0 2 2 2
endmodule
