// Logisim project 10-Score_calculator_test.circ as structural Verilog: 1 circuit, main circuit 分数计算器测试
module \分数计算器测试  (
  output [5:0] Cnt,
  output [1:0] S1,
  output [1:0] S2,
  output [1:0] S3,
  output [3:0] S,
  output _passed,
  output halt
);

  wire CLK, nhalt;
  wire [3:0] OutputS;

  Clock #(.highDuration(1), .lowDuration(1)) clock_1 (.out(CLK));
  Comparator #(.width(6), .mode("twosComplement")) comparator_1 (.a(Cnt), .b({6{1'b1}}), .eq(halt));  // open: gt, lt
  not not_1 (nhalt, halt);
  Counter #(.width(6), .max('h3f), .ongoal("wrap"), .trigger("rising"), .behavior("old")) counter_1 (
    .count(nhalt), .Q(Cnt), .clk(CLK));  // open: load, D, carry, clr, preset
  ROM #(.addrWidth(6), .dataWidth(2), .Select("low")) rom_1 (.addr(Cnt), .data(S1));
  ROM #(.addrWidth(6), .dataWidth(2), .Select("low")) rom_2 (.addr(Cnt), .data(S2));
  ROM #(.addrWidth(6), .dataWidth(2), .Select("low")) rom_3 (.addr(Cnt), .data(S3));
  ROM #(.addrWidth(6), .dataWidth(4), .Select("low")) rom_4 (.addr(Cnt), .data(OutputS));
  RAM #(.addrWidth(6), .dataWidth(4), .bus("separate"), .Select("low")) ram_1 (
    .addr(Cnt), .din(S), .str(nhalt), .clk(CLK));  // open: data, sel, ld, clr
  \分数计算器  \u_分数计算器_1  (.S1(S1), .S2(S2), .S3(S3), .S(S));
  Comparator #(.width(4), .mode("twosComplement")) comparator_2 (.a(S), .b(OutputS), .eq(_passed));  // open: gt, lt
  Pull_Resistor #(.pull(0)) pull_resistor_1 (.node(_passed));

  // Other names for the same wires on the sheet: Equal = _passed; Out[3:0] = S; tunnel[5:0] = Cnt

  // Notes on the sheet:
  //   contents of rom_1 (hex, n*v repeats v):
  //   0 1 2 3 0 1 2 3 0 1 2 3 0 1 2 3 0 1 2 3 0 1 2 3 0 1 2 3 0 1 2 3 0 1 2 3 0 1 2 3 0 1 2 3 0 1 2 3 0 1
  //   2 3 0 1 2 3 0 1 2 3 0 1 2 3
  //   contents of rom_2 (hex, n*v repeats v):
  //   4*0 4*1 4*2 4*3 4*0 4*1 4*2 4*3 4*0 4*1 4*2 4*3 4*0 4*1 4*2 4*3
  //   contents of rom_3 (hex, n*v repeats v):
  //   16*0 16*1 16*2 16*3
  //   contents of rom_4 (hex, n*v repeats v):
  //   0 1 2 3 1 2 3 4 2 3 4 5 3 4 5 6 1 2 3 4 2 3 4 5 3 4 5 6 4 5 6 7 2 3 4 5 3 4 5 6 4 5 6 7 5 6 7 8 3 4
  //   5 6 4 5 6 7 5 6 7 8 6 7 8 9
endmodule
