// Logisim project 11-4bit_Reg_test.circ as structural Verilog: 1 circuit, main circuit 4位并行加载寄存器测试
module \_4位并行加载寄存器测试  (
  output [5:0] Cnt,
  output [3:0] Din,
  output en,
  output rst,
  output [3:0] Q,
  output _passed,
  output halt
);

  wire CLK, nhalt;
  wire [3:0] OutputS;

  Clock #(.highDuration(1), .lowDuration(1)) clock_1 (.out(CLK));
  Comparator #(.width(6), .mode("twosComplement")) comparator_1 (.a(Cnt), .b({6{1'b1}}), .eq(halt));  // open: gt, lt
  not not_1 (nhalt, halt);
  Counter #(.width(6), .max('h3f), .ongoal("wrap"), .trigger("rising"), .behavior("old")) counter_1 (
    .count(nhalt), .Q(Cnt), .clk(CLK));  // open: load, D, carry, clr, preset
  ROM #(.addrWidth(6), .dataWidth(4), .Select("low")) rom_1 (.addr(Cnt), .data(Din));
  ROM #(.addrWidth(6), .dataWidth(1), .Select("low")) rom_2 (.addr(Cnt), .data(en));
  ROM #(.addrWidth(6), .dataWidth(1), .Select("low")) rom_3 (.addr(Cnt), .data(rst));
  ROM #(.addrWidth(6), .dataWidth(4), .Select("low")) rom_4 (.addr(Cnt), .data(OutputS));
  RAM #(.addrWidth(6), .dataWidth(4), .bus("separate"), .Select("low")) ram_1 (
    .addr(Cnt), .din(Q), .str(nhalt), .clk(CLK));  // open: data, sel, ld, clr
  \_4位并行加载寄存器  \u_4位并行加载寄存器_1  (.CLK(CLK), .Din(Din), .en(en), .Q(Q), .rst(rst));
  Comparator #(.width(4), .mode("twosComplement")) comparator_2 (.a(Q), .b(OutputS), .eq(_passed));  // open: gt, lt
  Pull_Resistor #(.pull(0)) pull_resistor_1 (.node(_passed));

  // Other names for the same wires on the sheet: Equal = _passed; Out[3:0] = Q; tunnel[5:0] = Cnt

  // Notes on the sheet:
  //   contents of rom_1 (hex, n*v repeats v):
  //   1 2 3 4 5 6 7 8 9 a b c d e f 0 1 2 3 4 5 6 7 8 9 a b c d e f 0 1 2 3 4 5 6 7 8 9 a b c d e f 0 1 2
  //   3 4 5 6 7 8 9 a b c d e f
  //   contents of rom_2 (hex, n*v repeats v):
  //   16*0 16*1 16*0 16*1
  //   contents of rom_3 (hex, n*v repeats v):
  //   32*0 32*1
  //   contents of rom_4 (hex, n*v repeats v):
  //   17*0 1 2 3 4 5 6 7 8 9 a b c d e f
endmodule
