// Logisim project 12-10x4bit_Reg_test.circ as structural Verilog: 1 circuit, main circuit 10*4bit存储器测试
module \_10_4bit存储器测试  (
  output [9:0] Cnt,
  output en,
  output [3:0] Din,
  output [3:0] Addr,
  output rst,
  output [3:0] Q,
  output _passed,
  output halt
);

  wire CLK, nhalt;
  wire [3:0] OutputS;

  Clock #(.highDuration(1), .lowDuration(1)) clock_1 (.out(CLK));
  Comparator #(.width(10), .mode("twosComplement")) comparator_1 (.a(Cnt), .b({10{1'b1}}), .eq(halt));  // open: gt, lt
  not not_1 (nhalt, halt);
  Counter #(.width(10), .max('h3ff), .ongoal("wrap"), .trigger("rising"), .behavior("old")) counter_1 (
    .count(nhalt), .Q(Cnt), .clk(CLK));  // open: load, D, carry, clr, preset
  ROM #(.addrWidth(10), .dataWidth(4), .Select("low")) rom_1 (.addr(Cnt), .data(Din));
  ROM #(.addrWidth(10), .dataWidth(1), .Select("low")) rom_2 (.addr(Cnt), .data(en));
  ROM #(.addrWidth(10), .dataWidth(1), .Select("low")) rom_3 (.addr(Cnt), .data(rst));
  ROM #(.addrWidth(10), .dataWidth(4), .Select("low")) rom_4 (.addr(Cnt), .data(Addr));
  ROM #(.addrWidth(10), .dataWidth(4), .Select("low")) rom_5 (.addr(Cnt), .data(OutputS));
  RAM #(.addrWidth(10), .dataWidth(4), .bus("separate"), .Select("low")) ram_1 (
    .addr(Cnt), .din(Q), .str(nhalt), .clk(CLK));  // open: data, sel, ld, clr
  \_10_4bit寄存器  \u_10_4bit寄存器_1  (.CLK(CLK), .Din(Din), .en(en), .Addr(Addr), .Q(Q), .rst(rst));
  Comparator #(.width(4), .mode("twosComplement")) comparator_2 (.a(Q), .b(OutputS), .eq(_passed));  // open: gt, lt
  Pull_Resistor #(.pull(0)) pull_resistor_1 (.node(_passed));

  // Other names for the same wires on the sheet: Equal = _passed; Out[3:0] = Q; tunnel[9:0] = Cnt

  // Notes on the sheet:
  //   contents of rom_1 (hex, n*v repeats v):
  //   1 2 3 4 5 6 7 8 9 a b c d e f 0 2 3 4 5 6 7 8 9 a b c d e f 0 1 3 4 5 6 7 8 9 a b c d e f 0 1 2 4 5
  //   6 7 8 9 a b c d e f 0 1 2 3 5 6 7 8 9 a b c d e f 0 1 2 3 4 6 7 8 9 a b c d e f 0 1 2 3 4 5 7 8 9 a
  //   b c d e f 0 1 2 3 4 5 6 8 9 a b c d e f 0 1 2 3 4 5 6 7 9 a b c d e f 0 1 2 3 4 5 6 7 8 a b c d e f
  //   0 1 2 3 4 5 6 7 8 9 b c d e f 0 1 2 3 4 5 6 7 8 9 a c d e f 0 1 2 3 4 5 6 7 8 9 a b d e f 0 1 2 3 4
  //   5 6 7 8 9 a b c e f 0 1 2 3 4 5 6 7 8 9 a b c d f 0 1 2 3 4 5 6 7 8 9 a b c d e 0 1 2 3 4 5 6 7 8 9
  //   a b c d e f 1 2 3 4 5 6 7 8 9 a b c d e f 0 2 3 4 5 6 7 8 9 a b c d e f 0 1 3 4 5 6 7 8 9 a b c d e
  //   f 0 1 2 4 5 6 7 8 9 a b c d e f 0 1 2 3 5 6 7 8 9 a b c d e f 0 1 2 3 4 6 7 8 9 a b c d e f 0 1 2 3
  //   4 5 7 8 9 a b c d e f 0 1 2 3 4 5 6 8 9 a b c d e f 0 1 2 3 4 5 6 7 9 a b c d e f 0 1 2 3 4 5 6 7 8
  //   a b c d e f 0 1 2 3 4 5 6 7 8 9 b c d e f 0 1 2 3 4 5 6 7 8 9 a c d e f 0 1 2 3 4 5 6 7 8 9 a b d e
  //   f 0 1 2 3 4 5 6 7 8 9 a b c e f 0 1 2 3 4 5 6 7 8 9 a b c d f 0 1 2 3 4 5 6 7 8 9 a b c d e 0 1 2 3
  //   4 5 6 7 8 9 a b c d e f 1 2 3 4 5 6 7 8 9 a b c d e f 0 2 3 4 5 6 7 8 9 a b c d e f 0 1 3 4 5 6 7 8
  //   9 a b c d e f 0 1 2 4 5 6 7 8 9 a b c d e f 0 1 2 3 5 6 7 8 9 a b c d e f 0 1 2 3 4 6 7 8 9 a b c d
  //   e f 0 1 2 3 4 5 7 8 9 a b c d e f 0 1 2 3 4 5 6 8 9 a b c d e f 0 1 2 3 4 5 6 7 9 a b c d e f 0 1 2
  //   3 4 5 6 7 8 a b c d e f 0 1 2 3 4 5 6 7 8 9 b c d e f 0 1 2 3 4 5 6 7 8 9 a c d e f 0 1 2 3 4 5 6 7
  //   8 9 a b d e f 0 1 2 3 4 5 6 7 8 9 a b c e f 0 1 2 3 4 5 6 7 8 9 a b c d f 0 1 2 3 4 5 6 7 8 9 a b c
  //   d e 0 1 2 3 4 5 6 7 8 9 a b c d e f 1 2 3 4 5 6 7 8 9 a b c d e f 0 2 3 4 5 6 7 8 9 a b c d e f 0 1
  //   3 4 5 6 7 8 9 a b c d e f 0 1 2 4 5 6 7 8 9 a b c d e f 0 1 2 3 5 6 7 8 9 a b c d e f 0 1 2 3 4 6 7
  //   8 9 a b c d e f 0 1 2 3 4 5 7 8 9 a b c d e f 0 1 2 3 4 5 6 8 9 a b c d e f 0 1 2 3 4 5 6 7 9 a b c
  //   d e f 0 1 2 3 4 5 6 7 8 a b c d e f 0 1 2 3 4 5 6 7 8 9 b c d e f 0 1 2 3 4 5 6 7 8 9 a c d e f 0 1
  //   2 3 4 5 6 7 8 9 a b d e f 0 1 2 3 4 5 6 7 8 9 a b c e f 0 1 2 3 4 5 6 7 8 9 a b c d f 0 1 2 3 4 5 6
  //   7 8 9 a b c d e 0 1 2 3 4 5 6 7 8 9 a b c d e f
  //   contents of rom_2 (hex, n*v repeats v):
  //   256*1 512*0 256*1
  //   contents of rom_3 (hex, n*v repeats v):
  //   512*0 512*1
  //   contents of rom_4 (hex, n*v repeats v):
  //   16*0 16*1 16*2 16*3 16*4 16*5 16*6 16*7 16*8 16*9 16*0 16*1 16*2 16*3 16*4 16*5 16*0 16*1 16*2 16*3
  //   16*4 16*5 16*6 16*7 16*8 16*9 16*0 16*1 16*2 16*3 16*4 16*5 16*0 16*1 16*2 16*3 16*4 16*5 16*6 16*7
  //   16*8 16*9 16*0 16*1 16*2 16*3 16*4 16*5 16*0 16*1 16*2 16*3 16*4 16*5 16*6 16*7 16*8 16*9 16*0 16*1
  //   16*2 16*3 16*4 16*5
  //   contents of rom_5 (hex, n*v repeats v):
  //   0 1 2 3 4 5 6 7 8 9 a b c d e f 0 2 3 4 5 6 7 8 9 a b c d e f 0 0 3 4 5 6 7 8 9 a b c d e f 0 1 0 4
  //   5 6 7 8 9 a b c d e f 0 1 2 0 5 6 7 8 9 a b c d e f 0 1 2 3 0 6 7 8 9 a b c d e f 0 1 2 3 4 0 7 8 9
  //   a b c d e f 0 1 2 3 4 5 0 8 9 a b c d e f 0 1 2 3 4 5 6 0 9 a b c d e f 0 1 2 3 4 5 6 7 0 a b c d e
  //   f 0 1 2 3 4 5 6 7 8 0 b c d e f 0 1 2 3 4 5 6 7 8 9 1 c d e f 0 1 2 3 4 5 6 7 8 9 a 2 d e f 0 1 2 3
  //   4 5 6 7 8 9 a b 3 e f 0 1 2 3 4 5 6 7 8 9 a b c 4 f 0 1 2 3 4 5 6 7 8 9 a b c d 5 0 1 2 3 4 5 6 7 8
  //   9 a b c d e 16*a 16*b 16*c 16*d 16*e 16*f 16*6 16*7 16*8 16*9 16*a 16*b 16*c 16*d 16*e 16*f
endmodule
