// Logisim project 13-Controller_FSM_test.circ as structural Verilog: 1 circuit, main circuit 控制电路状态转换测试
module \控制电路状态转换测试  (
  output [7:0] Cnt,
  output S0,
  output S1,
  output S2,
  output start,
  output over,
  output store,
  output show,
  output rst,
  output N0,
  output N1,
  output N2,
  output _passed,
  output halt
);

  wire CLK, nhalt;
  wire [2:0] OutputS;

  Clock #(.highDuration(1), .lowDuration(1)) clock_1 (.out(CLK));
  Comparator #(.width(8), .mode("twosComplement")) comparator_1 (.a(Cnt), .b({8{1'b1}}), .eq(halt));  // open: gt, lt
  not not_1 (nhalt, halt);
  Counter #(.width(8), .max('hff), .ongoal("wrap"), .trigger("rising"), .behavior("old")) counter_1 (
    .count(nhalt), .Q(Cnt), .clk(CLK));  // open: load, D, carry, clr, preset
  ROM #(.addrWidth(8), .dataWidth(8), .Select("low")) rom_1 (
    .addr(Cnt), .data({rst, show, store, over, start, S2, S1, S0}));
  ROM #(.addrWidth(8), .dataWidth(3), .Select("low")) rom_2 (.addr(Cnt), .data(OutputS));
  RAM #(.addrWidth(8), .dataWidth(3), .bus("separate"), .Select("low")) ram_1 (
    .addr(Cnt), .din({N2, N1, N0}), .str(nhalt), .clk(CLK));  // open: data, sel, ld, clr
  Comparator #(.width(3), .mode("twosComplement")) comparator_2 (
    .a({N2, N1, N0}), .b(OutputS), .eq(_passed));  // open: gt, lt
  \控制电路状态转换  \u_控制电路状态转换_1  (
    .S0(S0), .S1(S1), .S2(S2), .start(start), .over(over), .store(store), .show(show), .reset(rst), .N0(N0),
    .N1(N1), .N2(N2));
  Pull_Resistor #(.pull(0)) pull_resistor_1 (.node(_passed));

  // Other names for the same wires on the sheet: Equal = _passed;
  //   Input[7:0] = {rst, show, store, over, start, S2, S1, S0}; Out[2:0] = {N2, N1, N0}; tunnel[7:0] = Cnt

  // Notes on the sheet:
  //   contents of rom_1 (hex, n*v repeats v):
  //   0 1 2 3 4 5 6 7 8 9 a b c d e f 10 11 12 13 14 15 16 17 18 19 1a 1b 1c 1d 1e 1f 20 21 22 23 24 25 26
  //   27 28 29 2a 2b 2c 2d 2e 2f 30 31 32 33 34 35 36 37 38 39 3a 3b 3c 3d 3e 3f 40 41 42 43 44 45 46 47
  //   48 49 4a 4b 4c 4d 4e 4f 50 51 52 53 54 55 56 57 58 59 5a 5b 5c 5d 5e 5f 60 61 62 63 64 65 66 67 68
  //   69 6a 6b 6c 6d 6e 6f 70 71 72 73 74 75 76 77 78 79 7a 7b 7c 7d 7e 7f 80 81 82 83 84 85 86 87 88 89
  //   8a 8b 8c 8d 8e 8f 90 91 92 93 94 95 96 97 98 99 9a 9b 9c 9d 9e 9f a0 a1 a2 a3 a4 a5 a6 a7 a8 a9 aa
  //   ab ac ad ae af b0 b1 b2 b3 b4 b5 b6 b7 b8 b9 ba bb bc bd be bf c0 c1 c2 c3 c4 c5 c6 c7 c8 c9 ca cb
  //   cc cd ce cf d0 d1 d2 d3 d4 d5 d6 d7 d8 d9 da db dc dd de df e0 e1 e2 e3 e4 e5 e6 e7 e8 e9 ea eb ec
  //   ed ee ef f0 f1 f2 f3 f4 f5 f6 f7 f8 f9 fa fb fc fd fe ff
  //   contents of rom_2 (hex, n*v repeats v):
  //   1 1 2 3 4 5 0 0 1 2 2 3 4 5 0 0 1 1 3 3 4 5 0 0 1 2 3 3 4 5 0 0 1 1 2 4 4 4 0 0 1 2 2 4 4 4 0 0 1 1
  //   3 4 4 4 0 0 1 2 3 4 4 4 0 0 1 5 2 5 5 5 0 0 1 0 2 5 5 5 0 0 1 5 3 5 5 5 0 0 1 0 3 5 5 5 0 0 1 5 2 0
  //   5 0 0 0 1 0 2 0 5 0 0 0 1 5 3 0 5 0 0 0 1 0 3 0 5 0 0 0 1 7*0 1 7*0 1 7*0 1 7*0 1 7*0 1 7*0 1 7*0 1
  //   7*0 1 7*0 1 7*0 1 7*0 1 7*0 1 7*0 1 7*0 1 7*0 1
endmodule
