// Logisim project 14-Controller_outfunc_test.circ as structural Verilog: 1 circuit, main circuit 控制电路输出函数测试
module \控制电路输出函数测试  (
  output [2:0] Cnt,
  output S0,
  output S1,
  output S2,
  output TimeEn,
  output JudgeEn,
  output StoreEn,
  output ShowEn,
  output RST,
  output _passed,
  output halt
);

  wire CLK, nhalt;
  wire [4:0] OutputS;

  Clock #(.highDuration(1), .lowDuration(1)) clock_1 (.out(CLK));
  Comparator #(.width(3), .mode("twosComplement")) comparator_1 (.a(Cnt), .b(3'b111), .eq(halt));  // open: gt, lt
  not not_1 (nhalt, halt);
  Counter #(.width(3), .max('h7), .ongoal("wrap"), .trigger("rising"), .behavior("old")) counter_1 (
    .count(nhalt), .Q(Cnt), .clk(CLK));  // open: load, D, carry, clr, preset
  ROM #(.addrWidth(3), .dataWidth(3), .Select("low")) rom_1 (.addr(Cnt), .data({S2, S1, S0}));
  ROM #(.addrWidth(3), .dataWidth(5), .Select("low")) rom_2 (.addr(Cnt), .data(OutputS));
  RAM #(.addrWidth(3), .dataWidth(5), .bus("separate"), .Select("low")) ram_1 (
    .addr(Cnt), .din({RST, ShowEn, StoreEn, JudgeEn, TimeEn}), .str(nhalt), .clk(CLK));  // open: data, sel, ld, clr
  \控制电路输出函数  \u_控制电路输出函数_1  (
    .S0(S0), .TimeEn(TimeEn), .S1(S1), .JudgeEn(JudgeEn), .S2(S2), .StoreEn(StoreEn), .ShowEn(ShowEn),
    .RST(RST));
  Comparator #(.width(5), .mode("twosComplement")) comparator_2 (
    .a({RST, ShowEn, StoreEn, JudgeEn, TimeEn}), .b(OutputS), .eq(_passed));  // open: gt, lt
  Pull_Resistor #(.pull(0)) pull_resistor_1 (.node(_passed));

  // Other names for the same wires on the sheet: Equal = _passed; Input[2:0] = {S2, S1, S0};
  //   Out[4:0] = {RST, ShowEn, StoreEn, JudgeEn, TimeEn}; tunnel[2:0] = Cnt

  // Notes on the sheet:
  //   contents of rom_1 (hex, n*v repeats v):
  //   0 1 2 3 4 5 6 7
  //   contents of rom_2 (hex, n*v repeats v):
  //   10 0 3 0 4 8
endmodule
