// Logisim project 15-Controller_test.circ as structural Verilog: 1 circuit, main circuit 控制电路测试
module \控制电路测试  (
  output [5:0] Cnt,
  output start,
  output over,
  output store,
  output show,
  output rst,
  output TimeEn,
  output JudgeEn,
  output StoreEn,
  output ShowEn,
  output RST_2,
  output _passed,
  output halt
);

  wire CLK, clock_1_out, nhalt;
  wire [4:0] OutputS;

  Clock #(.highDuration(1), .lowDuration(1)) clock_1 (.out(clock_1_out));
  Comparator #(.width(6), .mode("twosComplement")) comparator_1 (.a(Cnt), .b({6{1'b1}}), .eq(halt));  // open: gt, lt
  and and_1 (CLK, nhalt, clock_1_out);
  not not_1 (nhalt, halt);
  Counter #(.width(6), .max('h3f), .ongoal("wrap"), .trigger("rising"), .behavior("old")) counter_1 (
    .count(nhalt), .Q(Cnt), .clk(CLK));  // open: load, D, carry, clr, preset
  ROM #(.addrWidth(6), .dataWidth(5), .Select("low")) rom_1 (.addr(Cnt), .data({rst, show, store, over, start}));
  ROM #(.addrWidth(6), .dataWidth(5), .Select("low")) rom_2 (.addr(Cnt), .data(OutputS));
  RAM #(.addrWidth(6), .dataWidth(5), .bus("separate"), .Select("low")) ram_1 (
    .addr(Cnt), .din({RST_2, ShowEn, StoreEn, JudgeEn, TimeEn}), .str(nhalt), .clk(CLK));  // open: data, sel, ld, clr
  Comparator #(.width(5), .mode("twosComplement")) comparator_2 (
    .a({RST_2, ShowEn, StoreEn, JudgeEn, TimeEn}), .b(OutputS), .eq(_passed));  // open: gt, lt
  \控制电路  \u_控制电路_1  (
    .CLK(CLK), .start(start), .over(over), .store(store), .show(show), .rst(rst), .TimeEn(TimeEn),
    .JudgeEn(JudgeEn), .StoreEn(StoreEn), .ShowEn(ShowEn), .RST_2(RST_2));
  Pull_Resistor #(.pull(0)) pull_resistor_1 (.node(_passed));

  // Other names for the same wires on the sheet: Equal = _passed; Input[4:0] = {rst, show, store, over, start};
  //   Out[4:0] = {RST_2, ShowEn, StoreEn, JudgeEn, TimeEn}; RST_t = RST_2; tunnel[5:0] = Cnt

  // Notes on the sheet:
  //   contents of rom_1 (hex, n*v repeats v):
  //   0 0 1 1 2 2 3 3 4 4 5 5 6 6 7 7 8 8 9 9 a a b b c c d d e e f f 10 10 11 11 12 12 13 13 14 14 15 15
  //   16 16 17 17 18 18 19 19 1a 1a 1b 1b 1c 1c 1d 1d 1e 1e 1f 1f
  //   contents of rom_2 (hex, n*v repeats v):
  //   10 0 0 3 3 4*0 8*4 8*8 10 0 10 0 8 10 0 10 0 10 0 10 0 10 0 10 0 10 0 10 0 10 0 10 0 10 0 10 0 10 0
  //   10 0 10 0 10 0 10
endmodule
