// Logisim project test.circ as structural Verilog: 15 circuits, main circuit 数码管驱动测试
module \灯效驱动测试  (
  output [1:0] Cnt,
  output S0,
  output S1,
  output L1,
  output L2,
  output _PASS,
  output halt
);

  wire CLK, nhalt;
  wire [1:0] OutputS;

  Clock #(.highDuration(1), .lowDuration(1)) clock_1 (.out(CLK));
  Comparator #(.width(2), .mode("twosComplement")) comparator_1 (.a(Cnt), .b(2'b11), .eq(halt));  // open: gt, lt
  not not_1 (nhalt, halt);
  Counter #(.width(2), .max('h3), .ongoal("wrap"), .trigger("rising"), .behavior("old")) counter_1 (
    .count(nhalt), .Q(Cnt), .clk(CLK));  // open: load, D, carry, clr, preset
  ROM #(.addrWidth(2), .dataWidth(2), .Select("low")) rom_1 (.addr(Cnt), .data({S1, S0}));
  ROM #(.addrWidth(2), .dataWidth(2), .Select("low")) rom_2 (.addr(Cnt), .data(OutputS));
  \灯效驱动  \u_灯效驱动_1  (.S0(S0), .L1(L1), .S1(S1), .L2(L2));
  Comparator #(.width(2), .mode("twosComplement")) comparator_2 (
    .a({L2, L1}), .b(OutputS), .eq(_PASS));  // open: gt, lt
  Pull_Resistor #(.pull(0)) pull_resistor_1 (.node(_PASS));

  // Other names for the same wires on the sheet: Equal = _PASS; Input[1:0] = {S1, S0}; Out[1:0] = {L2, L1};
  //   tunnel[1:0] = Cnt

  // Notes on the sheet:
  //   contents of rom_1 (hex, n*v repeats v):
  //   0 1 2 3
  //   contents of rom_2 (hex, n*v repeats v):
  //   0 1 3 3
endmodule

module \数码管驱动测试  (
  output [15:0] Cnt,
  output [3:0] BCD,
  output [6:0] _7Segs,
  output _PASS,
  output halt
);

  wire CLK, nhalt, \数码管驱动_2_seg_1 , \数码管驱动_2_seg_2 , \数码管驱动_2_seg_3 , \数码管驱动_2_seg_4 , \数码管驱动_2_seg_5 ,
       \数码管驱动_2_seg_6 , \数码管驱动_2_seg_7 ;
  wire [6:0] OutputS;

  Clock #(.highDuration(1), .lowDuration(1)) clock_1 (.out(CLK));
  Comparator #(.width(16), .mode("twosComplement")) comparator_1 (.a(Cnt), .b(16'h9), .eq(halt));  // open: gt, lt
  not not_1 (nhalt, halt);
  Counter #(.width(16), .max('ha), .ongoal("wrap"), .trigger("rising"), .behavior("old")) counter_1 (
    .count(nhalt), .Q(Cnt), .clk(CLK));  // open: load, D, carry, clr, preset
  ROM #(.addrWidth(16), .dataWidth(4), .Select("low")) rom_1 (.addr(Cnt), .data(BCD));
  ROM #(.addrWidth(16), .dataWidth(7), .Select("low")) rom_2 (.addr(Cnt), .data(OutputS));
  RAM #(.addrWidth(16), .dataWidth(7), .bus("separate"), .Select("low")) ram_1 (
    .addr(Cnt), .din(_7Segs), .str(nhalt), .clk(CLK));  // open: data, sel, ld, clr
  \数码管驱动  \u_数码管驱动_1  (
    .X0(BCD[0]), .X1(BCD[1]), .X2(BCD[2]), .seg_1(_7Segs[0]), .X3(BCD[3]), .seg_2(_7Segs[1]),
    .seg_3(_7Segs[2]), .seg_4(_7Segs[3]), .seg_5(_7Segs[4]), .seg_6(_7Segs[5]), .seg_7(_7Segs[6]));
  \数码管驱动  \u_数码管驱动_2  (
    .X0(BCD[0]), .X1(BCD[1]), .X2(BCD[2]), .seg_1(\数码管驱动_2_seg_1 ), .X3(BCD[3]), .seg_2(\数码管驱动_2_seg_2 ),
    .seg_3(\数码管驱动_2_seg_3 ), .seg_4(\数码管驱动_2_seg_4 ), .seg_5(\数码管驱动_2_seg_5 ), .seg_6(\数码管驱动_2_seg_6 ),
    .seg_7(\数码管驱动_2_seg_7 ));
  Comparator #(.width(7), .mode("twosComplement")) comparator_2 (.a(_7Segs), .b(OutputS), .eq(_PASS));  // open: gt, lt
  _7_Segment_Display #(.active("true")) u_7_segment_display_1 (
    .g(\数码管驱动_2_seg_1 ), .f(\数码管驱动_2_seg_2 ), .a(\数码管驱动_2_seg_3 ), .b(\数码管驱动_2_seg_4 ), .e(\数码管驱动_2_seg_5 ),
    .d(\数码管驱动_2_seg_6 ), .c(\数码管驱动_2_seg_7 ));  // open: dp
  Pull_Resistor #(.pull(0)) pull_resistor_1 (.node(_PASS));

  // Other names for the same wires on the sheet: Equal = _PASS; Input[3:0] = BCD; Out[6:0] = _7Segs;
  //   tunnel[15:0] = Cnt

  // Notes on the sheet:
  //   contents of rom_1 (hex, n*v repeats v):
  //   0 1 2 3 4 5 6 7 8 9
  //   contents of rom_2 (hex, n*v repeats v):
  //   7e 48 3d 6d 4b 67 77 4c 7f 6f
endmodule

module \二进制转BCD测试  (
  output [3:0] Cnt,
  output [3:0] Binary,
  output [3:0] BCD_0,
  output [3:0] BCD_1,
  output _PASS,
  output halt
);

  wire CLK, nhalt;
  wire [7:0] OutputS;

  Clock #(.highDuration(1), .lowDuration(1)) clock_1 (.out(CLK));
  Comparator #(.width(4), .mode("twosComplement")) comparator_1 (.a(Cnt), .b(4'b1111), .eq(halt));  // open: gt, lt
  not not_1 (nhalt, halt);
  Counter #(.width(4), .max('hf), .ongoal("wrap"), .trigger("rising"), .behavior("old")) counter_1 (
    .count(nhalt), .Q(Cnt), .clk(CLK));  // open: load, D, carry, clr, preset
  ROM #(.addrWidth(4), .dataWidth(4), .Select("low")) rom_1 (.addr(Cnt), .data(Binary));
  ROM #(.addrWidth(4), .dataWidth(8), .Select("low")) rom_2 (.addr(Cnt), .data(OutputS));
  RAM #(.addrWidth(4), .dataWidth(8), .bus("separate"), .Select("low")) ram_1 (
    .addr(Cnt), .din({BCD_1, BCD_0}), .str(nhalt), .clk(CLK));  // open: data, sel, ld, clr
  \二进制转BCD  \u_二进制转bcd_1  (.binary(Binary), .BCD_1(BCD_1), .BCD_0(BCD_0));
  Comparator #(.width(8), .mode("twosComplement")) comparator_2 (
    .a({BCD_1, BCD_0}), .b(OutputS), .eq(_PASS));  // open: gt, lt
  Pull_Resistor #(.pull(0)) pull_resistor_1 (.node(_PASS));

  // Other names for the same wires on the sheet: Equal = _PASS; Input[3:0] = Binary; Out[7:0] = {BCD_1, BCD_0};
  //   tunnel[3:0] = Cnt

  // Notes on the sheet:
  //   contents of rom_1 (hex, n*v repeats v):
  //   0 1 2 3 4 5 6 7 8 9 a b c d e f
  //   contents of rom_2 (hex, n*v repeats v):
  //   0 1 2 3 4 5 6 7 8 9 10 11 12 13 14 15
endmodule

module \BCD逆向计数器输出函数测试  (
  output [3:0] Cnt,
  output S3,
  output S2,
  output S1,
  output S0,
  output Cout,
  output _PASS,
  output halt
);

  wire CLK, nhalt, OutputS;

  Clock #(.highDuration(1), .lowDuration(1)) clock_1 (.out(CLK));
  Comparator #(.width(4), .mode("twosComplement")) comparator_1 (.a(Cnt), .b(4'b1111), .eq(halt));  // open: gt, lt
  not not_1 (nhalt, halt);
  Counter #(.width(4), .max('hf), .ongoal("wrap"), .trigger("rising"), .behavior("old")) counter_1 (
    .count(nhalt), .Q(Cnt), .clk(CLK));  // open: load, D, carry, clr, preset
  ROM #(.addrWidth(4), .dataWidth(4), .Select("low")) rom_1 (.addr(Cnt), .data({S0, S1, S2, S3}));
  ROM #(.addrWidth(4), .dataWidth(1), .Select("low")) rom_2 (.addr(Cnt), .data(OutputS));
  RAM #(.addrWidth(4), .dataWidth(1), .bus("separate"), .Select("low")) ram_1 (
    .addr(Cnt), .din(Cout), .str(nhalt), .clk(CLK));  // open: data, sel, ld, clr
  \BCD逆向计数器输出函数  \bcd逆向计数器输出函数_1  (.S3(S3), .Cout(Cout), .S2(S2), .S1(S1), .S0(S0));
  Comparator #(.width(1), .mode("twosComplement")) comparator_2 (.a(Cout), .b(OutputS), .eq(_PASS));  // open: gt, lt
  Pull_Resistor #(.pull(0)) pull_resistor_1 (.node(_PASS));

  // Other names for the same wires on the sheet: Equal = _PASS; Input[3:0] = {S0, S1, S2, S3}; Out = Cout;
  //   tunnel[3:0] = Cnt

  // Notes on the sheet:
  //   contents of rom_1 (hex, n*v repeats v):
  //   0 1 2 3 4 5 6 7 8 9 a b c d e f
  //   contents of rom_2 (hex, n*v repeats v):
  //   1
endmodule

module \BCD逆向计数器状态转换测试  (
  output [3:0] Cnt,
  output S3,
  output S2,
  output S1,
  output S0,
  output N3,
  output N2,
  output N1,
  output N0,
  output _PASS,
  output halt
);

  wire CLK, nhalt;
  wire [3:0] OutputS;

  Clock #(.highDuration(1), .lowDuration(1)) clock_1 (.out(CLK));
  Comparator #(.width(4), .mode("twosComplement")) comparator_1 (.a(Cnt), .b(4'b1111), .eq(halt));  // open: gt, lt
  not not_1 (nhalt, halt);
  Counter #(.width(4), .max('hf), .ongoal("wrap"), .trigger("rising"), .behavior("old")) counter_1 (
    .count(nhalt), .Q(Cnt), .clk(CLK));  // open: load, D, carry, clr, preset
  ROM #(.addrWidth(4), .dataWidth(4), .Select("low")) rom_1 (.addr(Cnt), .data({S3, S2, S1, S0}));
  ROM #(.addrWidth(4), .dataWidth(4), .Select("low")) rom_2 (.addr(Cnt), .data(OutputS));
  RAM #(.addrWidth(4), .dataWidth(4), .bus("separate"), .Select("low")) ram_1 (
    .addr(Cnt), .din({N3, N2, N1, N0}), .str(nhalt), .clk(CLK));  // open: data, sel, ld, clr
  \BCD逆向计数器状态转换  \bcd逆向计数器状态转换_1  (.S3(S3), .S2(S2), .S1(S1), .N3(N3), .S0(S0), .N2(N2), .N1(N1), .N0(N0));
  Comparator #(.width(4), .mode("twosComplement")) comparator_2 (
    .a({N3, N2, N1, N0}), .b(OutputS), .eq(_PASS));  // open: gt, lt
  Pull_Resistor #(.pull(0)) pull_resistor_1 (.node(_PASS));

  // Other names for the same wires on the sheet: Equal = _PASS; Input[3:0] = {S3, S2, S1, S0};
  //   Out[3:0] = {N3, N2, N1, N0}; tunnel[3:0] = Cnt

  // Notes on the sheet:
  //   contents of rom_1 (hex, n*v repeats v):
  //   0 1 2 3 4 5 6 7 8 9 a b c d e f
  //   contents of rom_2 (hex, n*v repeats v):
  //   9 0 1 2 3 4 5 6 7 8 f 2 7 4 7 6
endmodule

module \_4位BCD逆向计数器测试  (
  output [7:0] Cnt,
  output en,
  output rst,
  output [3:0] set,
  output [3:0] Q,
  output Cout,
  output _PASS,
  output halt
);

  wire CLK, nhalt;
  wire [4:0] OutputS;

  Clock #(.highDuration(1), .lowDuration(1)) clock_1 (.out(CLK));
  Comparator #(.width(8), .mode("twosComplement")) comparator_1 (.a(Cnt), .b({8{1'b1}}), .eq(halt));  // open: gt, lt
  not not_1 (nhalt, halt);
  Counter #(.width(8), .max('hff), .ongoal("wrap"), .trigger("rising"), .behavior("old")) counter_1 (
    .count(nhalt), .Q(Cnt), .clk(CLK));  // open: load, D, carry, clr, preset
  ROM #(.addrWidth(8), .dataWidth(4), .Select("low")) rom_1 (.addr(Cnt), .data(set));
  ROM #(.addrWidth(8), .dataWidth(1), .Select("low")) rom_2 (.addr(Cnt), .data(en));
  ROM #(.addrWidth(8), .dataWidth(1), .Select("low")) rom_3 (.addr(Cnt), .data(rst));
  ROM #(.addrWidth(8), .dataWidth(5), .Select("low")) rom_4 (.addr(Cnt), .data(OutputS));
  RAM #(.addrWidth(8), .dataWidth(5), .bus("separate"), .Select("low")) ram_1 (
    .addr(Cnt), .din({Cout, Q}), .str(nhalt), .clk(CLK));  // open: data, sel, ld, clr
  \_4位BCD逆向计数器  \u_4位bcd逆向计数器_1  (.CLK(CLK), .en(en), .rst(rst), .Q(Q), .Cout(Cout), .set(set));
  Comparator #(.width(5), .mode("twosComplement")) comparator_2 (
    .a({Cout, Q}), .b(OutputS), .eq(_PASS));  // open: gt, lt
  Pull_Resistor #(.pull(0)) pull_resistor_1 (.node(_PASS));

  // Other names for the same wires on the sheet: Equal = _PASS; Out[4:0] = {Cout, Q}; tunnel[7:0] = Cnt

  // Notes on the sheet:
  //   contents of rom_1 (hex, n*v repeats v):
  //   256*9
  //   contents of rom_2 (hex, n*v repeats v):
  //   128*0 128*1
  //   contents of rom_3 (hex, n*v repeats v):
  //   64*1 128*0 64*1
  //   contents of rom_4 (hex, n*v repeats v):
  //   129*9 8 7 6 5 4 3 2 1 10 9 8 7 6 5 4 3 2 1 10 9 8 7 6 5 4 3 2 1 10 9 8 7 6 5 4 3 2 1 10 9 8 7 6 5 4
  //   3 2 1 10 9 8 7 6 5 4 3 2 1 10 9 8 7 6 64*9
endmodule

module \计时器测试  (
  output [11:0] Cnt,
  output en,
  output rst,
  output [3:0] \time ,
  output [3:0] Q1,
  output [3:0] Q0,
  output zero,
  output _PASS,
  output halt
);

  wire CLK, nhalt;
  wire [8:0] OutputS;

  Clock #(.highDuration(1), .lowDuration(1)) clock_1 (.out(CLK));
  Comparator #(.width(12), .mode("twosComplement")) comparator_1 (.a(Cnt), .b(12'h7ff), .eq(halt));  // open: gt, lt
  not not_1 (nhalt, halt);
  Counter #(.width(12), .max('hfff), .ongoal("wrap"), .trigger("rising"), .behavior("old")) counter_1 (
    .count(nhalt), .Q(Cnt), .clk(CLK));  // open: load, D, carry, clr, preset
  ROM #(.addrWidth(12), .dataWidth(4), .Select("low")) rom_1 (.addr(Cnt), .data(\time ));
  ROM #(.addrWidth(12), .dataWidth(1), .Select("low")) rom_2 (.addr(Cnt), .data(en));
  ROM #(.addrWidth(12), .dataWidth(1), .Select("low")) rom_3 (.addr(Cnt), .data(rst));
  ROM #(.addrWidth(12), .dataWidth(9), .Select("low")) rom_4 (.addr(Cnt), .data(OutputS));
  RAM #(.addrWidth(12), .dataWidth(9), .bus("separate"), .Select("low")) ram_1 (
    .addr(Cnt), .din({zero, Q1, Q0}), .str(nhalt), .clk(CLK));  // open: data, sel, ld, clr
  \计时器  \u_计时器_1  (.CLK(CLK), .en(en), .rst(rst), .\time (\time ), .Q1(Q1), .Q0(Q0), .zero(zero));
  Comparator #(.width(9), .mode("twosComplement")) comparator_2 (
    .a({zero, Q1, Q0}), .b(OutputS), .eq(_PASS));  // open: gt, lt
  Pull_Resistor #(.pull(0)) pull_resistor_1 (.node(_PASS));

  // Other names for the same wires on the sheet: Equal = _PASS; Out[8:0] = {zero, Q1, Q0}; tunnel[11:0] = Cnt

  // Notes on the sheet:
  //   contents of rom_1 (hex, n*v repeats v):
  //   4096*5
  //   contents of rom_2 (hex, n*v repeats v):
  //   1024*0 1024*1
  //   contents of rom_3 (hex, n*v repeats v):
  //   512*1 1024*0 512*1
  //   contents of rom_4 (hex, n*v repeats v):
  //   1025*5 100*4 100*3 100*2 100*1 111*100 512*5
endmodule

module \分数锁存器状态转换测试  (
  output [3:0] Cnt,
  output S0,
  output S1,
  output B1,
  output B2,
  output N0,
  output N1,
  output _PASS,
  output halt
);

  wire CLK, nhalt;
  wire [1:0] OutputS;

  Clock #(.highDuration(1), .lowDuration(1)) clock_1 (.out(CLK));
  Comparator #(.width(4), .mode("twosComplement")) comparator_1 (.a(Cnt), .b(4'b1111), .eq(halt));  // open: gt, lt
  not not_1 (nhalt, halt);
  Counter #(.width(4), .max('hf), .ongoal("wrap"), .trigger("rising"), .behavior("old")) counter_1 (
    .count(nhalt), .Q(Cnt), .clk(CLK));  // open: load, D, carry, clr, preset
  ROM #(.addrWidth(4), .dataWidth(1), .Select("low")) rom_1 (.addr(Cnt), .data(S0));
  ROM #(.addrWidth(4), .dataWidth(1), .Select("low")) rom_2 (.addr(Cnt), .data(S1));
  ROM #(.addrWidth(4), .dataWidth(1), .Select("low")) rom_3 (.addr(Cnt), .data(B1));
  ROM #(.addrWidth(4), .dataWidth(1), .Select("low")) rom_4 (.addr(Cnt), .data(B2));
  ROM #(.addrWidth(4), .dataWidth(2), .Select("low")) rom_5 (.addr(Cnt), .data(OutputS));
  RAM #(.addrWidth(4), .dataWidth(2), .bus("separate"), .Select("low")) ram_1 (
    .addr(Cnt), .din({N1, N0}), .str(nhalt), .clk(CLK));  // open: data, sel, ld, clr
  \分数锁存器状态转换电路  \u_分数锁存器状态转换电路_1  (.S0(S0), .N0(N0), .S1(S1), .B1(B1), .B2(B2), .N1(N1));
  Comparator #(.width(2), .mode("twosComplement")) comparator_2 (
    .a({N1, N0}), .b(OutputS), .eq(_PASS));  // open: gt, lt
  Pull_Resistor #(.pull(0)) pull_resistor_1 (.node(_PASS));

  // Other names for the same wires on the sheet: Equal = _PASS; Out[1:0] = {N1, N0}; tunnel[3:0] = Cnt

  // Notes on the sheet:
  //   contents of rom_1 (hex, n*v repeats v):
  //   0 1 0 1 0 1 0 1 0 1 0 1 0 1 0 1
  //   contents of rom_2 (hex, n*v repeats v):
  //   0 0 1 1 0 0 1 1 0 0 1 1 0 0 1 1
  //   contents of rom_3 (hex, n*v repeats v):
  //   4*0 4*1 4*0 4*1
  //   contents of rom_4 (hex, n*v repeats v):
  //   8*0 8*1
  //   contents of rom_5 (hex, n*v repeats v):
  //   0 1 2 0 1 1 1 0 2 2 2
endmodule

module \分数锁存器测试  (
  output [3:0] Cnt,
  output en,
  output B1,
  output B2,
  output RST,
  output S0,
  output S1,
  output _PASS,
  output halt
);

  wire CLK, nhalt;
  wire [1:0] OutputS;

  Clock #(.highDuration(1), .lowDuration(1)) clock_1 (.out(CLK));
  Comparator #(.width(4), .mode("twosComplement")) comparator_1 (.a(Cnt), .b(4'b1111), .eq(halt));  // open: gt, lt
  not not_1 (nhalt, halt);
  Counter #(.width(4), .max('hf), .ongoal("wrap"), .trigger("rising"), .behavior("old")) counter_1 (
    .count(nhalt), .Q(Cnt), .clk(CLK));  // open: load, D, carry, clr, preset
  ROM #(.addrWidth(4), .dataWidth(1), .Select("low")) rom_1 (.addr(Cnt), .data(en));
  ROM #(.addrWidth(4), .dataWidth(1), .Select("low")) rom_2 (.addr(Cnt), .data(B1));
  ROM #(.addrWidth(4), .dataWidth(1), .Select("low")) rom_3 (.addr(Cnt), .data(B2));
  ROM #(.addrWidth(4), .dataWidth(1), .Select("low")) rom_4 (.addr(Cnt), .data(RST));
  ROM #(.addrWidth(4), .dataWidth(2), .Select("low")) rom_5 (.addr(Cnt), .data(OutputS));
  RAM #(.addrWidth(4), .dataWidth(2), .bus("separate"), .Select("low")) ram_1 (
    .addr(Cnt), .din({S1, S0}), .str(nhalt), .clk(CLK));  // open: data, sel, ld, clr
  \分数锁存器  \u_分数锁存器_1  (.CLK(CLK), .en(en), .B1(B1), .B2(B2), .RST(RST), .S0(S0), .S1(S1));
  Comparator #(.width(2), .mode("twosComplement")) comparator_2 (
    .a({S1, S0}), .b(OutputS), .eq(_PASS));  // open: gt, lt
  Pull_Resistor #(.pull(0)) pull_resistor_1 (.node(_PASS));

  // Other names for the same wires on the sheet: Equal = _PASS; Out[1:0] = {S1, S0}; tunnel[3:0] = Cnt

  // Notes on the sheet:
  //   contents of rom_1 (hex, n*v repeats v):
  //   0 1 0 1 0 1 0 1 0 1 0 1 0 1 0 1
  //   contents of rom_2 (hex, n*v repeats v):
  //   0 0 1 1 0 0 1 1 0 0 1 1 0 0 1 1
  //   contents of rom_3 (hex, n*v repeats v):
  //   4*0 4*1 4*0 4*1
  //   contents of rom_4 (hex, n*v repeats v):
  //   8*0 8*1
  //   contents of rom_5 (hex, n*v repeats v):
  //   4*0 1 1 2 2
endmodule

module \分数计算器测试  (
  output [5:0] Cnt,
  output [1:0] S1,
  output [1:0] S2,
  output [1:0] S3,
  output [3:0] S,
  output _PASS,
  output halt
);

  wire CLK, nhalt;
  wire [3:0] OutputS;

  Clock #(.highDuration(1), .lowDuration(1)) clock_1 (.out(CLK));
  Comparator #(.width(6), .mode("twosComplement")) comparator_1 (.a(Cnt), .b({6{1'b1}}), .eq(halt));  // open: gt, lt
  not not_1 (nhalt, halt);
  Counter #(.width(6), .max('h3f), .ongoal("wrap"), .trigger("rising"), .behavior("old")) counter_1 (
    .count(nhalt), .Q(Cnt), .clk(CLK));  // open: load, D, carry, clr, preset
  ROM #(.addrWidth(6), .dataWidth(2), .Select("low")) rom_1 (.addr(Cnt), .data(S1));
  ROM #(.addrWidth(6), .dataWidth(2), .Select("low")) rom_2 (.addr(Cnt), .data(S2));
  ROM #(.addrWidth(6), .dataWidth(2), .Select("low")) rom_3 (.addr(Cnt), .data(S3));
  ROM #(.addrWidth(6), .dataWidth(4), .Select("low")) rom_4 (.addr(Cnt), .data(OutputS));
  RAM #(.addrWidth(6), .dataWidth(4), .bus("separate"), .Select("low")) ram_1 (
    .addr(Cnt), .din(S), .str(nhalt), .clk(CLK));  // open: data, sel, ld, clr
  \分数计算器  \u_分数计算器_1  (.S1(S1), .S2(S2), .S3(S3), .S(S));
  Comparator #(.width(4), .mode("twosComplement")) comparator_2 (.a(S), .b(OutputS), .eq(_PASS));  // open: gt, lt
  Pull_Resistor #(.pull(0)) pull_resistor_1 (.node(_PASS));

  // Other names for the same wires on the sheet: Equal = _PASS; Out[3:0] = S; tunnel[5:0] = Cnt

  // Notes on the sheet:
  //   contents of rom_1 (hex, n*v repeats v):
  //   0 1 2 3 0 1 2 3 0 1 2 3 0 1 2 3 0 1 2 3 0 1 2 3 0 1 2 3 0 1 2 3 0 1 2 3 0 1 2 3 0 1 2 3 0 1 2 3 0 1
  //   2 3 0 1 2 3 0 1 2 3 0 1 2 3
  //   contents of rom_2 (hex, n*v repeats v):
  //   4*0 4*1 4*2 4*3 4*0 4*1 4*2 4*3 4*0 4*1 4*2 4*3 4*0 4*1 4*2 4*3
  //   contents of rom_3 (hex, n*v repeats v):
  //   16*0 16*1 16*2 16*3
  //   contents of rom_4 (hex, n*v repeats v):
  //   0 1 2 3 1 2 3 4 2 3 4 5 3 4 5 6 1 2 3 4 2 3 4 5 3 4 5 6 4 5 6 7 2 3 4 5 3 4 5 6 4 5 6 7 5 6 7 8 3 4
  //   5 6 4 5 6 7 5 6 7 8 6 7 8 9
endmodule

module \_4位并行加载寄存器测试  (
  output [5:0] Cnt,
  output [3:0] Din,
  output en,
  output rst,
  output [3:0] Q,
  output _PASS,
  output halt
);

  wire CLK, nhalt;
  wire [3:0] OutputS;

  Clock #(.highDuration(1), .lowDuration(1)) clock_1 (.out(CLK));
  Comparator #(.width(6), .mode("twosComplement")) comparator_1 (.a(Cnt), .b({6{1'b1}}), .eq(halt));  // open: gt, lt
  not not_1 (nhalt, halt);
  Counter #(.width(6), .max('h3f), .ongoal("wrap"), .trigger("rising"), .behavior("old")) counter_1 (
    .count(nhalt), .Q(Cnt), .clk(CLK));  // open: load, D, carry, clr, preset
  ROM #(.addrWidth(6), .dataWidth(4), .Select("low")) rom_1 (.addr(Cnt), .data(Din));
  ROM #(.addrWidth(6), .dataWidth(1), .Select("low")) rom_2 (.addr(Cnt), .data(en));
  ROM #(.addrWidth(6), .dataWidth(1), .Select("low")) rom_3 (.addr(Cnt), .data(rst));
  ROM #(.addrWidth(6), .dataWidth(4), .Select("low")) rom_4 (.addr(Cnt), .data(OutputS));
  RAM #(.addrWidth(6), .dataWidth(4), .bus("separate"), .Select("low")) ram_1 (
    .addr(Cnt), .din(Q), .str(nhalt), .clk(CLK));  // open: data, sel, ld, clr
  \_4位并行加载寄存器  \u_4位并行加载寄存器_1  (.CLK(CLK), .Din(Din), .en(en), .Q(Q), .rst(rst));
  Comparator #(.width(4), .mode("twosComplement")) comparator_2 (.a(Q), .b(OutputS), .eq(_PASS));  // open: gt, lt
  Pull_Resistor #(.pull(0)) pull_resistor_1 (.node(_PASS));

  // Other names for the same wires on the sheet: Equal = _PASS; Out[3:0] = Q; tunnel[5:0] = Cnt

  // Notes on the sheet:
  //   contents of rom_1 (hex, n*v repeats v):
  //   1 2 3 4 5 6 7 8 9 a b c d e f 0 1 2 3 4 5 6 7 8 9 a b c d e f 0 1 2 3 4 5 6 7 8 9 a b c d e f 0 1 2
  //   3 4 5 6 7 8 9 a b c d e f
  //   contents of rom_2 (hex, n*v repeats v):
  //   16*0 16*1 16*0 16*1
  //   contents of rom_3 (hex, n*v repeats v):
  //   32*0 32*1
  //   contents of rom_4 (hex, n*v repeats v):
  //   17*0 1 2 3 4 5 6 7 8 9 a b c d e f
endmodule

module \_10_4bit存储器测试  (
  output [9:0] Cnt,
  output en,
  output [3:0] Din,
  output [3:0] Addr,
  output rst,
  output [3:0] Q,
  output _PASS,
  output halt
);

  wire CLK, nhalt;
  wire [3:0] OutputS;

  Clock #(.highDuration(1), .lowDuration(1)) clock_1 (.out(CLK));
  Comparator #(.width(10), .mode("twosComplement")) comparator_1 (.a(Cnt), .b({10{1'b1}}), .eq(halt));  // open: gt, lt
  not not_1 (nhalt, halt);
  Counter #(.width(10), .max('h3ff), .ongoal("wrap"), .trigger("rising"), .behavior("old")) counter_1 (
    .count(nhalt), .Q(Cnt), .clk(CLK));  // open: load, D, carry, clr, preset
  ROM #(.addrWidth(10), .dataWidth(4), .Select("low")) rom_1 (.addr(Cnt), .data(Din));
  ROM #(.addrWidth(10), .dataWidth(1), .Select("low")) rom_2 (.addr(Cnt), .data(en));
  ROM #(.addrWidth(10), .dataWidth(1), .Select("low")) rom_3 (.addr(Cnt), .data(rst));
  ROM #(.addrWidth(10), .dataWidth(4), .Select("low")) rom_4 (.addr(Cnt), .data(Addr));
  ROM #(.addrWidth(10), .dataWidth(4), .Select("low")) rom_5 (.addr(Cnt), .data(OutputS));
  RAM #(.addrWidth(10), .dataWidth(4), .bus("separate"), .Select("low")) ram_1 (
    .addr(Cnt), .din(Q), .str(nhalt), .clk(CLK));  // open: data, sel, ld, clr
  \_10_4bit寄存器  \u_10_4bit寄存器_1  (.CLK(CLK), .Din(Din), .en(en), .Addr(Addr), .Q(Q), .rst(rst));
  Comparator #(.width(4), .mode("twosComplement")) comparator_2 (.a(Q), .b(OutputS), .eq(_PASS));  // open: gt, lt
  Pull_Resistor #(.pull(0)) pull_resistor_1 (.node(_PASS));

  // Other names for the same wires on the sheet: Equal = _PASS; Out[3:0] = Q; tunnel[9:0] = Cnt

  // Notes on the sheet:
  //   contents of rom_1 (hex, n*v repeats v):
  //   1 2 3 4 5 6 7 8 9 a b c d e f 0 2 3 4 5 6 7 8 9 a b c d e f 0 1 3 4 5 6 7 8 9 a b c d e f 0 1 2 4 5
  //   6 7 8 9 a b c d e f 0 1 2 3 5 6 7 8 9 a b c d e f 0 1 2 3 4 6 7 8 9 a b c d e f 0 1 2 3 4 5 7 8 9 a
  //   b c d e f 0 1 2 3 4 5 6 8 9 a b c d e f 0 1 2 3 4 5 6 7 9 a b c d e f 0 1 2 3 4 5 6 7 8 a b c d e f
  //   0 1 2 3 4 5 6 7 8 9 b c d e f 0 1 2 3 4 5 6 7 8 9 a c d e f 0 1 2 3 4 5 6 7 8 9 a b d e f 0 1 2 3 4
  //   5 6 7 8 9 a b c e f 0 1 2 3 4 5 6 7 8 9 a b c d f 0 1 2 3 4 5 6 7 8 9 a b c d e 0 1 2 3 4 5 6 7 8 9
  //   a b c d e f 1 2 3 4 5 6 7 8 9 a b c d e f 0 2 3 4 5 6 7 8 9 a b c d e f 0 1 3 4 5 6 7 8 9 a b c d e
  //   f 0 1 2 4 5 6 7 8 9 a b c d e f 0 1 2 3 5 6 7 8 9 a b c d e f 0 1 2 3 4 6 7 8 9 a b c d e f 0 1 2 3
  //   4 5 7 8 9 a b c d e f 0 1 2 3 4 5 6 8 9 a b c d e f 0 1 2 3 4 5 6 7 9 a b c d e f 0 1 2 3 4 5 6 7 8
  //   a b c d e f 0 1 2 3 4 5 6 7 8 9 b c d e f 0 1 2 3 4 5 6 7 8 9 a c d e f 0 1 2 3 4 5 6 7 8 9 a b d e
  //   f 0 1 2 3 4 5 6 7 8 9 a b c e f 0 1 2 3 4 5 6 7 8 9 a b c d f 0 1 2 3 4 5 6 7 8 9 a b c d e 0 1 2 3
  //   4 5 6 7 8 9 a b c d e f 1 2 3 4 5 6 7 8 9 a b c d e f 0 2 3 4 5 6 7 8 9 a b c d e f 0 1 3 4 5 6 7 8
  //   9 a b c d e f 0 1 2 4 5 6 7 8 9 a b c d e f 0 1 2 3 5 6 7 8 9 a b c d e f 0 1 2 3 4 6 7 8 9 a b c d
  //   e f 0 1 2 3 4 5 7 8 9 a b c d e f 0 1 2 3 4 5 6 8 9 a b c d e f 0 1 2 3 4 5 6 7 9 a b c d e f 0 1 2
  //   3 4 5 6 7 8 a b c d e f 0 1 2 3 4 5 6 7 8 9 b c d e f 0 1 2 3 4 5 6 7 8 9 a c d e f 0 1 2 3 4 5 6 7
  //   8 9 a b d e f 0 1 2 3 4 5 6 7 8 9 a b c e f 0 1 2 3 4 5 6 7 8 9 a b c d f 0 1 2 3 4 5 6 7 8 9 a b c
  //   d e 0 1 2 3 4 5 6 7 8 9 a b c d e f 1 2 3 4 5 6 7 8 9 a b c d e f 0 2 3 4 5 6 7 8 9 a b c d e f 0 1
  //   3 4 5 6 7 8 9 a b c d e f 0 1 2 4 5 6 7 8 9 a b c d e f 0 1 2 3 5 6 7 8 9 a b c d e f 0 1 2 3 4 6 7
  //   8 9 a b c d e f 0 1 2 3 4 5 7 8 9 a b c d e f 0 1 2 3 4 5 6 8 9 a b c d e f 0 1 2 3 4 5 6 7 9 a b c
  //   d e f 0 1 2 3 4 5 6 7 8 a b c d e f 0 1 2 3 4 5 6 7 8 9 b c d e f 0 1 2 3 4 5 6 7 8 9 a c d e f 0 1
  //   2 3 4 5 6 7 8 9 a b d e f 0 1 2 3 4 5 6 7 8 9 a b c e f 0 1 2 3 4 5 6 7 8 9 a b c d f 0 1 2 3 4 5 6
  //   7 8 9 a b c d e 0 1 2 3 4 5 6 7 8 9 a b c d e f
  //   contents of rom_2 (hex, n*v repeats v):
  //   256*1 512*0 256*1
  //   contents of rom_3 (hex, n*v repeats v):
  //   512*0 512*1
  //   contents of rom_4 (hex, n*v repeats v):
  //   16*0 16*1 16*2 16*3 16*4 16*5 16*6 16*7 16*8 16*9 16*0 16*1 16*2 16*3 16*4 16*5 16*0 16*1 16*2 16*3
  //   16*4 16*5 16*6 16*7 16*8 16*9 16*0 16*1 16*2 16*3 16*4 16*5 16*0 16*1 16*2 16*3 16*4 16*5 16*6 16*7
  //   16*8 16*9 16*0 16*1 16*2 16*3 16*4 16*5 16*0 16*1 16*2 16*3 16*4 16*5 16*6 16*7 16*8 16*9 16*0 16*1
  //   16*2 16*3 16*4 16*5
  //   contents of rom_5 (hex, n*v repeats v):
  //   0 1 2 3 4 5 6 7 8 9 a b c d e f 0 2 3 4 5 6 7 8 9 a b c d e f 0 0 3 4 5 6 7 8 9 a b c d e f 0 1 0 4
  //   5 6 7 8 9 a b c d e f 0 1 2 0 5 6 7 8 9 a b c d e f 0 1 2 3 0 6 7 8 9 a b c d e f 0 1 2 3 4 0 7 8 9
  //   a b c d e f 0 1 2 3 4 5 0 8 9 a b c d e f 0 1 2 3 4 5 6 0 9 a b c d e f 0 1 2 3 4 5 6 7 0 a b c d e
  //   f 0 1 2 3 4 5 6 7 8 0 b c d e f 0 1 2 3 4 5 6 7 8 9 1 c d e f 0 1 2 3 4 5 6 7 8 9 a 2 d e f 0 1 2 3
  //   4 5 6 7 8 9 a b 3 e f 0 1 2 3 4 5 6 7 8 9 a b c 4 f 0 1 2 3 4 5 6 7 8 9 a b c d 5 0 1 2 3 4 5 6 7 8
  //   9 a b c d e 16*a 16*b 16*c 16*d 16*e 16*f 16*6 16*7 16*8 16*9 16*a 16*b 16*c 16*d 16*e 16*f
endmodule

module \控制电路状态转换测试  (
  output [7:0] Cnt,
  output S0,
  output S1,
  output S2,
  output start,
  output over,
  output store,
  output show,
  output rst,
  output N0,
  output N1,
  output N2,
  output _PASS,
  output halt
);

  wire CLK, nhalt;
  wire [2:0] OutputS;

  Clock #(.highDuration(1), .lowDuration(1)) clock_1 (.out(CLK));
  Comparator #(.width(8), .mode("twosComplement")) comparator_1 (.a(Cnt), .b({8{1'b1}}), .eq(halt));  // open: gt, lt
  not not_1 (nhalt, halt);
  Counter #(.width(8), .max('hff), .ongoal("wrap"), .trigger("rising"), .behavior("old")) counter_1 (
    .count(nhalt), .Q(Cnt), .clk(CLK));  // open: load, D, carry, clr, preset
  ROM #(.addrWidth(8), .dataWidth(8), .Select("low")) rom_1 (
    .addr(Cnt), .data({rst, show, store, over, start, S2, S1, S0}));
  ROM #(.addrWidth(8), .dataWidth(3), .Select("low")) rom_2 (.addr(Cnt), .data(OutputS));
  RAM #(.addrWidth(8), .dataWidth(3), .bus("separate"), .Select("low")) ram_1 (
    .addr(Cnt), .din({N2, N1, N0}), .str(nhalt), .clk(CLK));  // open: data, sel, ld, clr
  Comparator #(.width(3), .mode("twosComplement")) comparator_2 (
    .a({N2, N1, N0}), .b(OutputS), .eq(_PASS));  // open: gt, lt
  \控制电路状态转换  \u_控制电路状态转换_1  (
    .S0(S0), .S1(S1), .S2(S2), .start(start), .over(over), .store(store), .show(show), .reset(rst), .N0(N0),
    .N1(N1), .N2(N2));
  Pull_Resistor #(.pull(0)) pull_resistor_1 (.node(_PASS));

  // Other names for the same wires on the sheet: Equal = _PASS;
  //   Input[7:0] = {rst, show, store, over, start, S2, S1, S0}; Out[2:0] = {N2, N1, N0}; tunnel[7:0] = Cnt

  // Notes on the sheet:
  //   contents of rom_1 (hex, n*v repeats v):
  //   0 1 2 3 4 5 6 7 8 9 a b c d e f 10 11 12 13 14 15 16 17 18 19 1a 1b 1c 1d 1e 1f 20 21 22 23 24 25 26
  //   27 28 29 2a 2b 2c 2d 2e 2f 30 31 32 33 34 35 36 37 38 39 3a 3b 3c 3d 3e 3f 40 41 42 43 44 45 46 47
  //   48 49 4a 4b 4c 4d 4e 4f 50 51 52 53 54 55 56 57 58 59 5a 5b 5c 5d 5e 5f 60 61 62 63 64 65 66 67 68
  //   69 6a 6b 6c 6d 6e 6f 70 71 72 73 74 75 76 77 78 79 7a 7b 7c 7d 7e 7f 80 81 82 83 84 85 86 87 88 89
  //   8a 8b 8c 8d 8e 8f 90 91 92 93 94 95 96 97 98 99 9a 9b 9c 9d 9e 9f a0 a1 a2 a3 a4 a5 a6 a7 a8 a9 aa
  //   ab ac ad ae af b0 b1 b2 b3 b4 b5 b6 b7 b8 b9 ba bb bc bd be bf c0 c1 c2 c3 c4 c5 c6 c7 c8 c9 ca cb
  //   cc cd ce cf d0 d1 d2 d3 d4 d5 d6 d7 d8 d9 da db dc dd de df e0 e1 e2 e3 e4 e5 e6 e7 e8 e9 ea eb ec
  //   ed ee ef f0 f1 f2 f3 f4 f5 f6 f7 f8 f9 fa fb fc fd fe ff
  //   contents of rom_2 (hex, n*v repeats v):
  //   1 1 2 3 4 5 0 0 1 2 2 3 4 5 0 0 1 1 3 3 4 5 0 0 1 2 3 3 4 5 0 0 1 1 2 4 4 4 0 0 1 2 2 4 4 4 0 0 1 1
  //   3 4 4 4 0 0 1 2 3 4 4 4 0 0 1 5 2 5 5 5 0 0 1 0 2 5 5 5 0 0 1 5 3 5 5 5 0 0 1 0 3 5 5 5 0 0 1 5 2 0
  //   5 0 0 0 1 0 2 0 5 0 0 0 1 5 3 0 5 0 0 0 1 0 3 0 5 0 0 0 1 7*0 1 7*0 1 7*0 1 7*0 1 7*0 1 7*0 1 7*0 1
  //   7*0 1 7*0 1 7*0 1 7*0 1 7*0 1 7*0 1 7*0 1 7*0 1
endmodule

module \控制电路输出函数测试  (
  output [2:0] Cnt,
  output S0,
  output S1,
  output S2,
  output TimeEn,
  output JudgeEn,
  output StoreEn,
  output ShowEn,
  output RST,
  output _PASS,
  output halt
);

  wire CLK, nhalt;
  wire [4:0] OutputS;

  Clock #(.highDuration(1), .lowDuration(1)) clock_1 (.out(CLK));
  Comparator #(.width(3), .mode("twosComplement")) comparator_1 (.a(Cnt), .b(3'b111), .eq(halt));  // open: gt, lt
  not not_1 (nhalt, halt);
  Counter #(.width(3), .max('h7), .ongoal("wrap"), .trigger("rising"), .behavior("old")) counter_1 (
    .count(nhalt), .Q(Cnt), .clk(CLK));  // open: load, D, carry, clr, preset
  ROM #(.addrWidth(3), .dataWidth(3), .Select("low")) rom_1 (.addr(Cnt), .data({S2, S1, S0}));
  ROM #(.addrWidth(3), .dataWidth(5), .Select("low")) rom_2 (.addr(Cnt), .data(OutputS));
  RAM #(.addrWidth(3), .dataWidth(5), .bus("separate"), .Select("low")) ram_1 (
    .addr(Cnt), .din({RST, ShowEn, StoreEn, JudgeEn, TimeEn}), .str(nhalt), .clk(CLK));  // open: data, sel, ld, clr
  \控制电路输出函数  \u_控制电路输出函数_1  (
    .S0(S0), .TimeEn(TimeEn), .S1(S1), .JudgeEn(JudgeEn), .S2(S2), .StoreEn(StoreEn), .ShowEn(ShowEn),
    .RST(RST));
  Comparator #(.width(5), .mode("twosComplement")) comparator_2 (
    .a({RST, ShowEn, StoreEn, JudgeEn, TimeEn}), .b(OutputS), .eq(_PASS));  // open: gt, lt
  Pull_Resistor #(.pull(0)) pull_resistor_1 (.node(_PASS));

  // Other names for the same wires on the sheet: Equal = _PASS; Input[2:0] = {S2, S1, S0};
  //   Out[4:0] = {RST, ShowEn, StoreEn, JudgeEn, TimeEn}; tunnel[2:0] = Cnt

  // Notes on the sheet:
  //   contents of rom_1 (hex, n*v repeats v):
  //   0 1 2 3 4 5 6 7
  //   contents of rom_2 (hex, n*v repeats v):
  //   10 0 3 0 4 8
endmodule

module \控制电路测试  (
  output [5:0] Cnt,
  output start,
  output over,
  output store,
  output show,
  output rst,
  output TimeEn,
  output JudgeEn,
  output StoreEn,
  output ShowEn,
  output RST_2,
  output _PASS,
  output halt
);

  wire CLK, clock_1_out, nhalt;
  wire [4:0] OutputS;

  Clock #(.highDuration(1), .lowDuration(1)) clock_1 (.out(clock_1_out));
  Comparator #(.width(6), .mode("twosComplement")) comparator_1 (.a(Cnt), .b({6{1'b1}}), .eq(halt));  // open: gt, lt
  and and_1 (CLK, nhalt, clock_1_out);
  not not_1 (nhalt, halt);
  Counter #(.width(6), .max('h3f), .ongoal("wrap"), .trigger("rising"), .behavior("old")) counter_1 (
    .count(nhalt), .Q(Cnt), .clk(CLK));  // open: load, D, carry, clr, preset
  ROM #(.addrWidth(6), .dataWidth(5), .Select("low")) rom_1 (.addr(Cnt), .data({rst, show, store, over, start}));
  ROM #(.addrWidth(6), .dataWidth(5), .Select("low")) rom_2 (.addr(Cnt), .data(OutputS));
  RAM #(.addrWidth(6), .dataWidth(5), .bus("separate"), .Select("low")) ram_1 (
    .addr(Cnt), .din({RST_2, ShowEn, StoreEn, JudgeEn, TimeEn}), .str(nhalt), .clk(CLK));  // open: data, sel, ld, clr
  Comparator #(.width(5), .mode("twosComplement")) comparator_2 (
    .a({RST_2, ShowEn, StoreEn, JudgeEn, TimeEn}), .b(OutputS), .eq(_PASS));  // open: gt, lt
  \控制电路  \u_控制电路_1  (
    .CLK(CLK), .start(start), .over(over), .store(store), .show(show), .rst(rst), .TimeEn(TimeEn),
    .JudgeEn(JudgeEn), .StoreEn(StoreEn), .ShowEn(ShowEn), .RST_2(RST_2));
  Pull_Resistor #(.pull(0)) pull_resistor_1 (.node(_PASS));

  // Other names for the same wires on the sheet: Equal = _PASS; Input[4:0] = {rst, show, store, over, start};
  //   Out[4:0] = {RST_2, ShowEn, StoreEn, JudgeEn, TimeEn}; RST_t = RST_2; tunnel[5:0] = Cnt

  // Notes on the sheet:
  //   contents of rom_1 (hex, n*v repeats v):
  //   0 0 1 1 2 2 3 3 4 4 5 5 6 6 7 7 8 8 9 9 a a b b c c d d e e f f 10 10 11 11 12 12 13 13 14 14 15 15
  //   16 16 17 17 18 18 19 19 1a 1a 1b 1b 1c 1c 1d 1d 1e 1e 1f 1f
  //   contents of rom_2 (hex, n*v repeats v):
  //   10 0 0 3 3 4*0 8*4 8*8 10 0 10 0 8 10 0 10 0 10 0 10 0 10 0 10 0 10 0 10 0 10 0 10 0 10 0 10 0 10 0
  //   10 0 10 0 10 0 10
endmodule
